// Digital circuit A Register.dig as structural Verilog
module A_Register (
  input  BUS__0,
  input  BUS__1,
  input  BUS__2,
  input  BUS__3,
  input  BUS__4,
  input  BUS__5,
  input  BUS__6,
  input  BUS__7,
  input  CLK,
  input  A1__hat,
  input  CLR,
  input  A0__hat,
  output A__0,
  output A__1,
  output A__2,
  output A__3,
  output A__4,
  output A__5,
  output A__6,
  output A__7
);

  _74245 _74245_1 (
    .pin1(1'b1), .pin2(A__7), .pin3(A__6), .pin4(A__5), .pin5(A__4), .pin6(A__3), .pin7(A__2), .pin8(A__1),
    .pin9(A__0), .pin10(1'b0), .pin11(BUS__0), .pin12(BUS__1), .pin13(BUS__2), .pin14(BUS__3),
    .pin15(BUS__4), .pin16(BUS__5), .pin17(BUS__6), .pin18(BUS__7), .pin19(A0__hat), .pin20(1'b1));
  _74173 _74173_1 (
    .pin1(1'b0), .pin2(1'b0), .pin3(A__7), .pin4(A__6), .pin5(A__5), .pin6(A__4), .pin7(CLK), .pin8(1'b0),
    .pin9(A1__hat), .pin10(A1__hat), .pin11(BUS__4), .pin12(BUS__5), .pin13(BUS__6), .pin14(BUS__7),
    .pin15(CLR), .pin16(1'b1));
  LED led_1 (.in(A__7));
  LED led_2 (.in(A__6));
  LED led_3 (.in(A__5));
  LED led_4 (.in(A__4));
  LED led_5 (.in(A__3));
  _74173 _74173_2 (
    .pin1(1'b0), .pin2(1'b0), .pin3(A__3), .pin4(A__2), .pin5(A__1), .pin6(A__0), .pin7(CLK), .pin8(1'b0),
    .pin9(A1__hat), .pin10(A1__hat), .pin11(BUS__0), .pin12(BUS__1), .pin13(BUS__2), .pin14(BUS__3),
    .pin15(CLR), .pin16(1'b1));
  LED led_6 (.in(A__2));
  LED led_7 (.in(A__1));
  LED led_8 (.in(A__0));
endmodule
