// Digital circuit Arithmetic Logic Unit.dig as structural Verilog
module Arithmetic_Logic_Unit (
  input  FI__hat,
  input  CLK,
  input  CLR,
  input  A__7,
  input  A__6,
  input  A__5,
  input  A__4,
  input  A__3,
  input  A__2,
  input  A__1,
  input  A__0,
  input  B__7,
  input  B__6,
  input  B__5,
  input  B__4,
  input  B__3,
  input  B__2,
  input  B__1,
  input  B__0,
  input  EO__hat,
  input  SU,
  output CF,
  output ZF,
  output BUS__0,
  output BUS__1,
  output BUS__2,
  output BUS__3,
  output BUS__4,
  output BUS__5,
  output BUS__6,
  output BUS__7
);

  wire notconnected_1_out, notconnected_2_out, U19_pin14, U20_pin2, U20_pin6, U20_pin7, U20_pin11, U20_pin15,
       U21_pin2, U21_pin6, U21_pin11, U21_pin15, U22_pin2, U22_pin3, U22_pin5, U22_pin6, U22_pin8, U22_pin9,
       U22_pin11, U22_pin12, U23_pin1, U23_pin2, U23_pin3, U23_pin5, U23_pin6, U23_pin9, U23_pin10,
       U23_pin12, U23_pin13;

  _7408 U23 (
    .pin1(U23_pin1), .pin2(U23_pin2), .pin3(U23_pin3), .pin4(U23_pin3), .pin5(U23_pin5), .pin6(U23_pin6),
    .pin7(1'b0), .pin8(U23_pin5), .pin9(U23_pin9), .pin10(U23_pin10), .pin12(U23_pin12), .pin13(U23_pin13),
    .pin14(1'b1));  // open: pin11
  // NotConnected on notconnected_1_out
  // NotConnected on notconnected_2_out
  // NotConnected on U23_pin13
  // NotConnected on U23_pin12
  LED led_1 (.in(CF));
  LED led_2 (.in(ZF));
  _74173 U19 (
    .pin1(1'b0), .pin2(1'b0), .pin3(CF), .pin4(ZF), .pin7(CLK), .pin8(1'b0), .pin9(FI__hat), .pin10(FI__hat),
    .pin11(notconnected_1_out), .pin12(notconnected_2_out), .pin13(U23_pin6), .pin14(U19_pin14), .pin15(CLR),
    .pin16(1'b1));  // open: pin5, pin6
  _7402 U22 (
    .pin1(U23_pin1), .pin2(U22_pin2), .pin3(U22_pin3), .pin4(U23_pin2), .pin5(U22_pin5), .pin6(U22_pin6),
    .pin7(1'b0), .pin8(U22_pin8), .pin9(U22_pin9), .pin10(U23_pin9), .pin11(U22_pin11), .pin12(U22_pin12),
    .pin13(U23_pin10), .pin14(1'b1));
  _74245 U17 (
    .pin1(1'b1), .pin2(U22_pin2), .pin3(U22_pin3), .pin4(U22_pin5), .pin5(U22_pin6), .pin6(U22_pin8),
    .pin7(U22_pin9), .pin8(U22_pin11), .pin9(U22_pin12), .pin10(1'b0), .pin11(BUS__0), .pin12(BUS__1),
    .pin13(BUS__2), .pin14(BUS__3), .pin15(BUS__4), .pin16(BUS__5), .pin17(BUS__6), .pin18(BUS__7),
    .pin19(EO__hat), .pin20(1'b1));
  LED led_3 (.in(U22_pin12));
  LED led_4 (.in(U22_pin11));
  LED led_5 (.in(U22_pin9));
  LED led_6 (.in(U22_pin8));
  LED led_7 (.in(U22_pin6));
  LED led_8 (.in(U22_pin5));
  LED led_9 (.in(U22_pin3));
  LED led_10 (.in(U22_pin2));
  _74283 U20 (
    .pin1(U22_pin5), .pin2(U20_pin2), .pin3(A__5), .pin4(U22_pin6), .pin5(A__4), .pin6(U20_pin6),
    .pin7(U20_pin7), .pin8(1'b0), .pin9(U19_pin14), .pin10(U22_pin2), .pin11(U20_pin11), .pin12(A__7),
    .pin13(U22_pin3), .pin14(A__6), .pin15(U20_pin15), .pin16(1'b1));
  _74283 U21 (
    .pin1(U22_pin11), .pin2(U21_pin2), .pin3(A__1), .pin4(U22_pin12), .pin5(A__0), .pin6(U21_pin6),
    .pin7(SU), .pin8(1'b0), .pin9(U20_pin7), .pin10(U22_pin8), .pin11(U21_pin11), .pin12(A__3),
    .pin13(U22_pin9), .pin14(A__2), .pin15(U21_pin15), .pin16(1'b1));
  _7486 U16 (
    .pin1(B__5), .pin2(SU), .pin3(U20_pin2), .pin4(B__4), .pin5(SU), .pin6(U20_pin6), .pin7(1'b0),
    .pin8(U20_pin11), .pin9(B__7), .pin10(SU), .pin11(U20_pin15), .pin12(B__6), .pin13(SU), .pin14(1'b1));
  _7486 U18 (
    .pin1(B__1), .pin2(SU), .pin3(U21_pin2), .pin4(B__0), .pin5(SU), .pin6(U21_pin6), .pin7(1'b0),
    .pin8(U21_pin11), .pin9(B__3), .pin10(SU), .pin11(U21_pin15), .pin12(B__2), .pin13(SU), .pin14(1'b1));

  // Notes on the sheet:
  //   Flags register
  //   ALU
endmodule
