// Digital circuit B Register.dig as structural Verilog
module B_Register (
  input  BUS__0,
  input  BUS__1,
  input  BUS__2,
  input  BUS__3,
  input  BUS__4,
  input  BUS__5,
  input  BUS__6,
  input  BUS__7,
  input  B1__hat,
  input  CLR,
  input  B0__hat,
  input  CLK,
  output B__0,
  output B__1,
  output B__2,
  output B__3,
  output B__4,
  output B__5,
  output B__6,
  output B__7
);

  _74245 _74245_1 (
    .pin1(1'b1), .pin2(B__7), .pin3(B__6), .pin4(B__5), .pin5(B__4), .pin6(B__3), .pin7(B__2), .pin8(B__1),
    .pin9(B__0), .pin10(1'b0), .pin11(BUS__0), .pin12(BUS__1), .pin13(BUS__2), .pin14(BUS__3),
    .pin15(BUS__4), .pin16(BUS__5), .pin17(BUS__6), .pin18(BUS__7), .pin19(B0__hat), .pin20(1'b1));
  _74173 _74173_1 (
    .pin1(1'b0), .pin2(1'b0), .pin3(B__7), .pin4(B__6), .pin5(B__5), .pin6(B__4), .pin7(CLK), .pin8(1'b0),
    .pin9(B1__hat), .pin10(B1__hat), .pin11(BUS__4), .pin12(BUS__5), .pin13(BUS__6), .pin14(BUS__7),
    .pin15(CLR), .pin16(1'b1));
  LED led_1 (.in(B__0));
  LED led_2 (.in(B__1));
  LED led_3 (.in(B__2));
  LED led_4 (.in(B__3));
  LED led_5 (.in(B__4));
  _74173 _74173_2 (
    .pin1(1'b0), .pin2(1'b0), .pin3(B__3), .pin4(B__2), .pin5(B__1), .pin6(B__0), .pin7(CLK), .pin8(1'b0),
    .pin9(B1__hat), .pin10(B1__hat), .pin11(BUS__0), .pin12(BUS__1), .pin13(BUS__2), .pin14(BUS__3),
    .pin15(CLR), .pin16(1'b1));
  LED led_6 (.in(B__5));
  LED led_7 (.in(B__6));
  LED led_8 (.in(B__7));
endmodule
