// Digital circuit CPU Control Logic.dig as structural Verilog
module CPU_Control_Logic (
  input  CF,
  input  ZF,
  input  IR__4,
  input  IR__5,
  input  IR__6,
  input  IR__7,
  input  CLK__hat,
  output CLR__hat,
  output CLR,
  output HLT,
  output MI__hat,
  output RI,
  output RO__hat,
  output IO__hat,
  output II__hat,
  output AI__hat,
  output AO__hat,
  output EO__hat,
  output SU,
  output BI__hat,
  output OI,
  output CE,
  output CO__hat,
  output J__hat,
  output FI__hat
);

  wire U47_p1, U48_p1, U48_p2, U48_p3, U48_p4;

  LED led_1 (.in(U48_p1));
  LED led_2 (.in(U48_p2));
  LED led_3 (.in(U48_p3));
  LED led_4 (.in(U48_p4));
  // _74161 U48: pin names not known; wires that end beside it: U48_p1, U48_p2, U48_p3, U48_p4
  // _74138 U50: pin names not known; wires that end beside it: IR__4, IR__5
  // _7400 U51: pin names not known; wires that end beside it: IR__6, IR__7
  LED led_5 ();  // open: in
  LED led_6 ();  // open: in
  LED led_7 ();  // open: in
  LED led_8 (.in(U47_p1));
  LED led_9 ();  // open: in
  LED led_10 ();  // open: in
  // _28c16 U47: pin names not known; wires that end beside it: U47_p1
  // _28c16 U52: pin names not known; wires that end beside it: CF, ZF
  LED led_11 ();  // open: in
  LED led_12 ();  // open: in
  LED led_13 ();  // open: in
  LED led_14 ();  // open: in
  LED led_15 ();  // open: in
  LED led_16 ();  // open: in
  LED led_17 ();  // open: in
  LED led_18 ();  // open: in
  LED led_19 ();  // open: in
  LED led_20 ();  // open: in
  LED led_21 ();  // open: in
  LED led_22 ();  // open: in
  LED led_23 ();  // open: in
  // _7404 U49: pin names not known; wires that end beside it: MI__hat
  // _7404 U53: pin names not known; wires that end beside it: J__hat
endmodule
