// Digital circuit Clock.dig as structural Verilog
module Clock (
  input  U1,
  input  HLT,
  output CLK__hat,
  output CLK
);

  wire notconnected_1_out, notconnected_2_out, notconnected_6_out, notconnected_7_out, U4_pin1, U4_pin2,
       U4_pin8, U4_pin11, U5_pin1, U5_pin3, U5_pin6, U5_pin9, U5_pin12, U5_pin13, U6_pin9, U6_pin10,
       U6_pin12, U6_pin13;

  // NotConnected on notconnected_1_out
  // NotConnected on notconnected_2_out
  _7404 U4 (
    .pin1(U4_pin1), .pin2(U4_pin2), .pin3(notconnected_1_out), .pin5(notconnected_2_out), .pin7(1'b0),
    .pin8(U4_pin8), .pin9(HLT), .pin11(U4_pin11), .pin12(CLK__hat), .pin13(CLK), .pin14(1'b1));  // open: pin4, pin6, pin10
  // NotConnected on U4_pin11
  // SwitchDT STEP__MODE: pin names not known; wires that end beside it: U4_pin1, 1'b1, 1'b0
  _7408 U5 (
    .pin1(U5_pin1), .pin2(U4_pin1), .pin3(U5_pin3), .pin4(U4_pin2), .pin5(U1), .pin6(U5_pin6), .pin7(1'b0),
    .pin8(CLK), .pin9(U5_pin9), .pin10(U4_pin8), .pin12(U5_pin12), .pin13(U5_pin13), .pin14(1'b1));  // open: pin11
  Button STEP__PULSE (.out(U5_pin1));
  // NotConnected on U5_pin13
  // NotConnected on U5_pin12
  // NotConnected on notconnected_6_out
  // NotConnected on notconnected_7_out
  _7432 U6 (
    .pin1(U5_pin3), .pin2(U5_pin6), .pin3(U5_pin9), .pin4(notconnected_6_out), .pin5(notconnected_7_out),
    .pin7(1'b0), .pin9(U6_pin9), .pin10(U6_pin10), .pin12(U6_pin12), .pin13(U6_pin13), .pin14(1'b1));  // open: pin6, pin8, pin11
  LED led_1 (.in(CLK));
  // NotConnected on U6_pin13
  // NotConnected on U6_pin12
  // NotConnected on U6_pin10
  // NotConnected on U6_pin9
endmodule
