// Digital circuit Computer.dig as structural Verilog
module Computer (
  input  MUX__CLK,
  input  U1
);

  wire DEC__HEX_p1, not_1_out, notconnected_33_out, notconnected_34_out, notconnected_39_out,
       notconnected_40_out, PROG__DATA__1_out, PROG__DATA__2_out, PROG__DATA__3_out, PROG__WRITE_p1, U4_pin1,
       U4_pin2, U4_pin3, U4_pin5, U4_pin8, U4_pin11, U5_pin1, U5_pin3, U5_pin6, U5_pin9, U5_pin12, U5_pin13,
       U6_pin4, U6_pin5, U6_pin9, U6_pin10, U6_pin12, U6_pin13, U7_pin2, U7_pin3, U7_pin4, U7_pin5, U7_pin6,
       U7_pin7, U7_pin8, U7_pin9, U10_pin2, U10_pin3, U10_pin4, U10_pin5, U10_pin6, U10_pin7, U10_pin8,
       U10_pin9, U10_pin19, U13_pin6, U13_pin7, U13_pin8, U13_pin9, U13_pin19, U14_pin9, U19_pin14, U20_pin2,
       U20_pin6, U20_pin7, U20_pin11, U20_pin15, U21_pin2, U21_pin6, U21_pin11, U21_pin15, U22_pin2,
       U22_pin3, U22_pin5, U22_pin6, U22_pin8, U22_pin9, U22_pin11, U22_pin12, U23_pin1, U23_pin2, U23_pin3,
       U23_pin5, U23_pin6, U23_pin9, U23_pin10, U23_pin12, U23_pin13, U24_pin1, U24_pin4, U24_pin5, U24_pin6,
       U24_pin7, U24_pin9, U24_pin10, U24_pin11, U24_pin12, U24_pin13, U24_pin14, U24_pin15, U25_pin4,
       U25_pin6, U25_pin10, U25_pin12, U26_pin2, U26_pin5, U26_pin11, U26_pin14, U27_pin11, U28_pin2,
       U28_pin4, U28_pin6, U28_pin8, U28_pin11, U28_pin13, U29_pin1, U29_pin2, U29_pin3, U29_pin4, U29_pin5,
       U29_pin6, U29_pin9, U29_pin11, U29_pin12, U29_pin13, U30_pin11, U30_pin12, U30_pin13, U30_pin14,
       U30_pin15, U30_pin16, U30_pin17, U30_pin18, U30_pin19, U31_pin1, U31_pin2, U31_pin4, U31_pin5,
       U31_pin9, U31_pin10, U31_pin12, U31_pin13, U32_pin1, U32_pin2, U32_pin3, U32_pin5, U32_pin6,
       U32_pin10, U32_pin11, U32_pin12, U32_pin13, U33_pin2, U33_pin3, U33_pin5, U33_pin6, U33_pin10,
       U33_pin11, U33_pin13, U33_pin14, U35_pin7, U36_pin11, U36_pin12, U36_pin13, U36_pin14, U38_pin4,
       U38_pin5, U38_pin6, U38_pin7, U38_pin13, U38_pin14, U38_pin15, U44_pin2, U44_pin5, U44_pin6, U44_pin9,
       U44_pin12, U44_pin15, U44_pin16, U44_pin19, U45_p9, U45_p10, U45_p11, U45_p14, U45_p15, U45_p20,
       U45_p21, U45_p22, U46_pin1, U46_pin3, U46_pin9, U46_pin10, U46_pin12, U46_pin13, U47_p2, U47_p3,
       U47_p4, U47_p5, U47_p9, U47_p10, U47_p11, U47_p14, U47_p15, U47_p20, U47_p21, U48_pin1, U48_pin2,
       U48_pin3, U48_pin4, U48_pin5, U48_pin6, U48_pin12, U48_pin13, U48_pin14, U49_pin2, U49_pin3, U49_pin5,
       U49_pin8, U49_pin10, U50_pin7, U50_pin9, U50_pin10, U50_pin11, U50_pin12, U50_pin13, U50_pin14,
       U50_pin15, U51_pin1, U51_pin4, U51_pin9, U51_pin11, U52_p9, U52_p10, U52_p11, U52_p20, U52_p21,
       U52_p22, U53_pin2, U53_pin4, U53_pin6, U53_pin9, U53_pin10, U53_pin12, undriven, undriven_2;

  // SwitchDT PROG__WRITE: pin names not known; wires that end beside it: PROG__WRITE_p1, 1'b1, 1'b0
  _74157 U32 (
    .pin1(U32_pin1), .pin2(U32_pin2), .pin3(U32_pin3), .pin5(U32_pin5), .pin6(U32_pin6), .pin8(1'b0),
    .pin10(U32_pin10), .pin11(U32_pin11), .pin12(U32_pin12), .pin13(U32_pin13), .pin14(PROG__WRITE_p1),
    .pin15(1'b0), .pin16(1'b1));  // open: pin4, pin7, pin9
  // NotConnected on U32_pin2
  _74189 U24 (
    .pin1(U24_pin1), .pin2(1'b0), .pin3(U32_pin12), .pin4(U24_pin4), .pin5(U24_pin5), .pin6(U24_pin6),
    .pin7(U24_pin7), .pin8(1'b0), .pin9(U24_pin9), .pin10(U24_pin10), .pin11(U24_pin11), .pin12(U24_pin12),
    .pin13(U24_pin13), .pin14(U24_pin14), .pin15(U24_pin15), .pin16(1'b1));
  // NotConnected on U32_pin3
  // NotConnected on U32_pin11
  // NotConnected on U32_pin5
  // NotConnected on U32_pin6
  _7400 U31 (
    .pin1(U31_pin1), .pin2(U31_pin2), .pin3(U32_pin13), .pin4(U31_pin4), .pin5(U31_pin5), .pin7(1'b0),
    .pin9(U31_pin9), .pin10(U31_pin10), .pin12(U31_pin12), .pin13(U31_pin13), .pin14(1'b1));  // open: pin6, pin8, pin11
  _7404 U28 (
    .pin1(U24_pin5), .pin2(U28_pin2), .pin3(U24_pin7), .pin4(U28_pin4), .pin5(U24_pin9), .pin6(U28_pin6),
    .pin7(1'b0), .pin8(U28_pin8), .pin9(U24_pin11), .pin11(U28_pin11), .pin13(U28_pin13), .pin14(1'b1));  // open: pin10, pin12
  // NotConnected on U32_pin10
  // NotConnected on U31_pin13
  // NotConnected on U31_pin12
  // NotConnected on U28_pin13
  // NotConnected on U31_pin10
  // NotConnected on U31_pin4
  // NotConnected on U31_pin5
  // NotConnected on U28_pin11
  // NotConnected on U31_pin9
  LED RAM__DATA__7 (.in(U28_pin2));
  LED T6 (.in(U50_pin9));
  LED T5 (.in(U50_pin10));
  LED T4 (.in(U50_pin11));
  LED T3 (.in(U50_pin12));
  LED T2 (.in(U50_pin13));
  LED T1 (.in(U50_pin14));
  LED T0 (.in(U50_pin15));
  _74161 U48 (
    .pin1(U48_pin1), .pin2(U48_pin2), .pin3(U48_pin3), .pin4(U48_pin4), .pin5(U48_pin5), .pin6(U48_pin6),
    .pin7(1'b1), .pin8(1'b0), .pin9(1'b1), .pin10(1'b1), .pin12(U48_pin12), .pin13(U48_pin13),
    .pin14(U48_pin14), .pin16(1'b1));  // open: pin11, pin15
  // NotConnected on U48_pin3
  // NotConnected on U48_pin4
  // NotConnected on U48_pin5
  // NotConnected on U48_pin6
  _74138 U50 (
    .pin1(U48_pin14), .pin2(U48_pin13), .pin3(U48_pin12), .pin4(1'b0), .pin5(1'b0), .pin6(1'b1),
    .pin7(U50_pin7), .pin8(1'b0), .pin9(U50_pin9), .pin10(U50_pin10), .pin11(U50_pin11), .pin12(U50_pin12),
    .pin13(U50_pin13), .pin14(U50_pin14), .pin15(U50_pin15), .pin16(1'b1));
  _7400 U51 (
    .pin1(U51_pin1), .pin2(U51_pin1), .pin3(U48_pin1), .pin4(U51_pin4), .pin5(U50_pin7), .pin6(U51_pin1),
    .pin7(1'b0), .pin8(U51_pin4), .pin9(U51_pin9), .pin10(U51_pin9), .pin11(U51_pin11), .pin12(U51_pin4),
    .pin13(U51_pin4), .pin14(1'b1));
  _7404 U29 (
    .pin1(U29_pin1), .pin2(U29_pin2), .pin3(U29_pin3), .pin4(U29_pin4), .pin5(U29_pin5), .pin6(U29_pin6),
    .pin7(1'b0), .pin9(U29_pin9), .pin11(U29_pin11), .pin12(U29_pin12), .pin13(U29_pin13), .pin14(1'b1));  // open: pin8, pin10
  LED RAM__DATA__6 (.in(U28_pin4));
  LED RAM__DATA__5 (.in(U28_pin6));
  // SwitchDT RESET: pin names not known; wires that end beside it: U51_pin9, 1'b1, 1'b0
  // NotConnected on U29_pin11
  LED RAM__DATA__4 (.in(U28_pin8));
  LED RAM__DATA__3 (.in(U29_pin12));
  // NotConnected on U29_pin9
  LED RAM__DATA__2 (.in(U29_pin2));
  LED RAM__DATA__1 (.in(U29_pin4));
  LED STEP__0 (.in(U48_pin14));
  LED STEP__1 (.in(U48_pin13));
  LED STEP__2 (.in(U48_pin12));
  LED RAM__DATA__0 (.in(U29_pin6));
  _74189 U25 (
    .pin1(U24_pin1), .pin2(1'b0), .pin3(U32_pin12), .pin4(U25_pin4), .pin5(U29_pin5), .pin6(U25_pin6),
    .pin7(U29_pin3), .pin8(1'b0), .pin9(U29_pin1), .pin10(U25_pin10), .pin11(U29_pin13), .pin12(U25_pin12),
    .pin13(U24_pin13), .pin14(U24_pin14), .pin15(U24_pin15), .pin16(1'b1));
  _74245 U30 (
    .pin1(1'b1), .pin2(U28_pin2), .pin3(U28_pin4), .pin4(U28_pin6), .pin5(U28_pin8), .pin6(U29_pin12),
    .pin7(U29_pin2), .pin8(U29_pin4), .pin9(U29_pin6), .pin10(1'b0), .pin11(U30_pin11), .pin12(U30_pin12),
    .pin13(U30_pin13), .pin14(U30_pin14), .pin15(U30_pin15), .pin16(U30_pin16), .pin17(U30_pin17),
    .pin18(U30_pin18), .pin19(U30_pin19), .pin20(1'b1));
  LED HLT (.in(U47_p20));
  LED MI (.in(U47_p21));
  _74245 U13 (
    .pin1(1'b1), .pin2(1'b0), .pin3(1'b0), .pin4(1'b0), .pin5(1'b0), .pin6(U13_pin6), .pin7(U13_pin7),
    .pin8(U13_pin8), .pin9(U13_pin9), .pin10(1'b0), .pin11(U30_pin11), .pin12(U30_pin12), .pin13(U30_pin13),
    .pin14(U30_pin14), .pin15(U30_pin15), .pin16(U30_pin16), .pin17(U30_pin17), .pin18(U30_pin18),
    .pin19(U13_pin19), .pin20(1'b1));
  LED RI (.in(U31_pin2));
  LED RO (.in(U49_pin3));
  // _28c16 U47: pin names not known; wires that end beside it: 1'b1, U47_p2, U47_p3, U47_p4, U47_p5, U48_pin12, U48_pin13, U48_pin14, U47_p9, U47_p10, U47_p11, 1'b0, 1'b1, U47_p14, U47_p15, 1'b1, 1'b0, 1'b0, 1'b0, U47_p20, U47_p21, U31_pin2
  // _28c16 U52: pin names not known; wires that end beside it: 1'b1, U47_p2, U47_p3, U47_p4, U47_p5, U48_pin12, U48_pin13, U48_pin14, U52_p9, U52_p10, U52_p11, 1'b0, 1'b1, U47_p14, U47_p15, 1'b1, 1'b0, 1'b0, 1'b0, U52_p20, U52_p21, U52_p22
  LED IO (.in(U49_pin5));
  LED II (.in(U47_p11));
  not not_1 (not_1_out, U32_pin1);
  // SwitchDT PROG__ADDR: pin names not known; wires that end beside it: U32_pin1, 1'b0, 1'b1
  LED AI (.in(U47_p10));
  LED AO (.in(U47_p9));
  LED PROG (.in(not_1_out));
  LED PROG__hat (.in(U32_pin1));
  LED EO (.in(U52_p20));
  LED SU (.in(U52_p21));
  _74157 U26 (
    .pin1(U32_pin1), .pin2(U26_pin2), .pin3(U30_pin18), .pin4(U24_pin4), .pin5(U26_pin5), .pin6(U30_pin17),
    .pin7(U24_pin6), .pin8(1'b0), .pin9(U24_pin12), .pin10(U30_pin15), .pin11(U26_pin11), .pin12(U24_pin10),
    .pin13(U30_pin16), .pin14(U26_pin14), .pin15(1'b0), .pin16(1'b1));
  LED BI (.in(U52_p22));
  LED OI (.in(U46_pin1));
  LED CE (.in(U35_pin7));
  LED CO (.in(U52_p11));
  _74173 U14 (
    .pin1(1'b0), .pin2(1'b0), .pin3(U47_p2), .pin4(U47_p3), .pin5(U47_p4), .pin6(U47_p5), .pin7(U31_pin1),
    .pin8(1'b0), .pin9(U14_pin9), .pin10(U14_pin9), .pin11(U30_pin15), .pin12(U30_pin16), .pin13(U30_pin17),
    .pin14(U30_pin18), .pin15(U51_pin11), .pin16(1'b1));
  LED J (.in(U52_p10));
  LED FI (.in(U52_p9));
  _7404 U4 (
    .pin1(U4_pin1), .pin2(U4_pin2), .pin3(U4_pin3), .pin5(U4_pin5), .pin7(1'b0), .pin8(U4_pin8),
    .pin9(U47_p20), .pin11(U4_pin11), .pin12(U48_pin2), .pin13(U31_pin1), .pin14(1'b1));  // open: pin4, pin6, pin10
  // NotConnected on U4_pin3
  // NotConnected on U4_pin5
  LED A3 (.in(U24_pin13));
  _74157 U33 (
    .pin1(U32_pin1), .pin2(U33_pin2), .pin3(U33_pin3), .pin4(U24_pin13), .pin5(U33_pin5), .pin6(U33_pin6),
    .pin7(U24_pin14), .pin8(1'b0), .pin9(U24_pin1), .pin10(U33_pin10), .pin11(U33_pin11), .pin12(U24_pin15),
    .pin13(U33_pin13), .pin14(U33_pin14), .pin15(1'b0), .pin16(1'b1));
  DipSwitch PROG__ADDR__A3 (.out(U33_pin2));
  LED A2 (.in(U24_pin14));
  LED A1 (.in(U24_pin15));
  DipSwitch PROG__ADDR__A2 (.out(U33_pin5));
  DipSwitch PROG__ADDR__A0 (.out(U33_pin11));
  DipSwitch PROG__ADDR__A1 (.out(U33_pin14));
  DipSwitch PROG__DATA__7 (.out(U26_pin2));
  DipSwitch PROG__DATA__6 (.out(U26_pin5));
  DipSwitch PROG__DATA__5 (.out(U26_pin14));
  LED IR__7 (.in(U47_p2));
  LED IR__6 (.in(U47_p3));
  // NotConnected on U4_pin11
  LED A0 (.in(U24_pin1));
  DipSwitch PROG__DATA__4 (.out(U26_pin11));
  DipSwitch PROG__DATA__3 (.out(PROG__DATA__3_out));
  DipSwitch PROG__DATA__2 (.out(PROG__DATA__2_out));
  DipSwitch PROG__DATA__1 (.out(PROG__DATA__1_out));
  LED IR__5 (.in(U47_p4));
  LED IR__4 (.in(U47_p5));
  _7404 U49 (
    .pin1(U47_p21), .pin2(U49_pin2), .pin3(U49_pin3), .pin4(U30_pin19), .pin5(U49_pin5), .pin6(U13_pin19),
    .pin7(1'b0), .pin8(U49_pin8), .pin9(U47_p9), .pin10(U49_pin10), .pin11(U47_p10), .pin12(U14_pin9),
    .pin13(U47_p11), .pin14(1'b1));
  _74157 U27 (
    .pin1(U32_pin1), .pin2(PROG__DATA__3_out), .pin3(U30_pin14), .pin4(U25_pin12), .pin5(PROG__DATA__2_out),
    .pin6(U30_pin13), .pin7(U25_pin10), .pin8(1'b0), .pin9(U25_pin4), .pin10(U30_pin11), .pin11(U27_pin11),
    .pin12(U25_pin6), .pin13(U30_pin12), .pin14(PROG__DATA__1_out), .pin15(1'b0), .pin16(1'b1));
  DipSwitch PROG__DATA__0 (.out(U27_pin11));
  _74173 U15 (
    .pin1(1'b0), .pin2(1'b0), .pin3(U13_pin6), .pin4(U13_pin7), .pin5(U13_pin8), .pin6(U13_pin9),
    .pin7(U31_pin1), .pin8(1'b0), .pin9(U14_pin9), .pin10(U14_pin9), .pin11(U30_pin11), .pin12(U30_pin12),
    .pin13(U30_pin13), .pin14(U30_pin14), .pin15(U51_pin11), .pin16(1'b1));
  LED IR__3 (.in(U13_pin6));
  LED IR__2 (.in(U13_pin7));
  LED IR__1 (.in(U13_pin8));
  LED IR__0 (.in(U13_pin9));
  // SwitchDT STEP__MODE: pin names not known; wires that end beside it: U4_pin1, 1'b1, 1'b0
  _7408 U5 (
    .pin1(U5_pin1), .pin2(U4_pin1), .pin3(U5_pin3), .pin4(U4_pin2), .pin5(U1), .pin6(U5_pin6), .pin7(1'b0),
    .pin8(U31_pin1), .pin9(U5_pin9), .pin10(U4_pin8), .pin12(U5_pin12), .pin13(U5_pin13), .pin14(1'b1));  // open: pin11
  _7404 U53 (
    .pin1(U52_p20), .pin2(U53_pin2), .pin3(U52_p22), .pin4(U53_pin4), .pin5(U52_p9), .pin6(U53_pin6),
    .pin7(1'b0), .pin9(U53_pin9), .pin10(U53_pin10), .pin11(U52_p10), .pin12(U53_pin12), .pin13(U52_p11),
    .pin14(1'b1));  // open: pin8
  _74173 U34 (
    .pin1(1'b0), .pin2(1'b0), .pin3(U33_pin3), .pin4(U33_pin6), .pin5(U33_pin13), .pin6(U33_pin10),
    .pin7(U31_pin1), .pin8(1'b0), .pin9(U49_pin2), .pin10(U49_pin2), .pin11(U30_pin11), .pin12(U30_pin12),
    .pin13(U30_pin13), .pin14(U30_pin14), .pin15(U51_pin11), .pin16(1'b1));
  // NotConnected on U5_pin13
  // NotConnected on U5_pin12
  // NotConnected on U53_pin9
  Button STEP__PULSE (.out(U5_pin1));
  _7432 U6 (
    .pin1(U5_pin3), .pin2(U5_pin6), .pin3(U5_pin9), .pin4(U6_pin4), .pin5(U6_pin5), .pin7(1'b0),
    .pin9(U6_pin9), .pin10(U6_pin10), .pin12(U6_pin12), .pin13(U6_pin13), .pin14(1'b1));  // open: pin6, pin8, pin11
  // NotConnected on U6_pin4
  // NotConnected on U6_pin5
  LED CLK (.in(U31_pin1));
  // NotConnected on U6_pin13
  // NotConnected on U6_pin12
  // NotConnected on U6_pin10
  // NotConnected on U6_pin9
  LED BUS__7 (.in(U30_pin18));
  LED BUS__6 (.in(U30_pin17));
  LED BUS__5 (.in(U30_pin16));
  LED BUS__4 (.in(U30_pin15));
  LED BUS__3 (.in(U30_pin14));
  LED BUS__2 (.in(U30_pin13));
  LED BUS__1 (.in(U30_pin12));
  LED BUS__0 (.in(U30_pin11));
  _74245 U36 (
    .pin1(1'b0), .pin6(U30_pin14), .pin7(U30_pin13), .pin8(U30_pin12), .pin9(U30_pin11), .pin10(1'b0),
    .pin11(U36_pin11), .pin12(U36_pin12), .pin13(U36_pin13), .pin14(U36_pin14), .pin19(U53_pin12),
    .pin20(1'b1));  // open: pin2, pin3, pin4, pin5, pin15, pin16, pin17, pin18
  // SwitchDT DEC__HEX: pin names not known; wires that end beside it: DEC__HEX_p1, 1'b1, 1'b0
  _74245 U7 (
    .pin1(1'b1), .pin2(U7_pin2), .pin3(U7_pin3), .pin4(U7_pin4), .pin5(U7_pin5), .pin6(U7_pin6),
    .pin7(U7_pin7), .pin8(U7_pin8), .pin9(U7_pin9), .pin10(1'b0), .pin11(U30_pin11), .pin12(U30_pin12),
    .pin13(U30_pin13), .pin14(U30_pin14), .pin15(U30_pin15), .pin16(U30_pin16), .pin17(U30_pin17),
    .pin18(U30_pin18), .pin19(U49_pin8), .pin20(1'b1));
  // NotConnected on notconnected_33_out
  // NotConnected on notconnected_34_out
  _74245 U10 (
    .pin1(1'b1), .pin2(U10_pin2), .pin3(U10_pin3), .pin4(U10_pin4), .pin5(U10_pin5), .pin6(U10_pin6),
    .pin7(U10_pin7), .pin8(U10_pin8), .pin9(U10_pin9), .pin10(1'b0), .pin11(U30_pin11), .pin12(U30_pin12),
    .pin13(U30_pin13), .pin14(U30_pin14), .pin15(U30_pin15), .pin16(U30_pin16), .pin17(U30_pin17),
    .pin18(U30_pin18), .pin19(U10_pin19), .pin20(1'b1));
  _7408 U46 (
    .pin1(U46_pin1), .pin2(U31_pin1), .pin3(U46_pin3), .pin4(notconnected_33_out),
    .pin5(notconnected_34_out), .pin7(1'b0), .pin9(U46_pin9), .pin10(U46_pin10), .pin12(U46_pin12),
    .pin13(U46_pin13), .pin14(1'b1));  // open: pin6, pin8, pin11
  LED PC__3 (.in(U36_pin14));
  LED PC__2 (.in(U36_pin13));
  // NotConnected on U46_pin13
  // NotConnected on U46_pin12
  // NotConnected on U46_pin10
  // NotConnected on U46_pin9
  LED PC__1 (.in(U36_pin12));
  LED PC__0 (.in(U36_pin11));
  _74161 U35 (
    .pin1(U51_pin4), .pin2(U31_pin1), .pin3(U30_pin11), .pin4(U30_pin12), .pin5(U30_pin13), .pin6(U30_pin14),
    .pin7(U35_pin7), .pin8(1'b0), .pin9(U53_pin10), .pin10(U35_pin7), .pin11(U36_pin14), .pin12(U36_pin13),
    .pin13(U36_pin12), .pin14(U36_pin11), .pin16(1'b1));  // open: pin15
  _7408 U23 (
    .pin1(U23_pin1), .pin2(U23_pin2), .pin3(U23_pin3), .pin4(U23_pin3), .pin5(U23_pin5), .pin6(U23_pin6),
    .pin7(1'b0), .pin8(U23_pin5), .pin9(U23_pin9), .pin10(U23_pin10), .pin12(U23_pin12), .pin13(U23_pin13),
    .pin14(1'b1));  // open: pin11
  _74173 U8 (
    .pin1(1'b0), .pin2(1'b0), .pin3(U7_pin2), .pin4(U7_pin3), .pin5(U7_pin4), .pin6(U7_pin5),
    .pin7(U31_pin1), .pin8(1'b0), .pin9(U49_pin10), .pin10(U49_pin10), .pin11(U30_pin15), .pin12(U30_pin16),
    .pin13(U30_pin17), .pin14(U30_pin18), .pin15(U51_pin11), .pin16(1'b1));
  // NotConnected on notconnected_39_out
  // NotConnected on notconnected_40_out
  // NotConnected on U23_pin13
  // NotConnected on U23_pin12
  _74273 U44 (
    .pin1(U51_pin4), .pin2(U44_pin2), .pin3(U30_pin11), .pin4(U30_pin12), .pin5(U44_pin5), .pin6(U44_pin6),
    .pin7(U30_pin13), .pin8(U30_pin14), .pin9(U44_pin9), .pin10(1'b0), .pin11(U46_pin3), .pin12(U44_pin12),
    .pin13(U30_pin15), .pin14(U30_pin16), .pin15(U44_pin15), .pin16(U44_pin16), .pin17(U30_pin17),
    .pin18(U30_pin18), .pin19(U44_pin19), .pin20(1'b1));
  _74173 U11 (
    .pin1(1'b0), .pin2(1'b0), .pin3(U10_pin2), .pin4(U10_pin3), .pin5(U10_pin4), .pin6(U10_pin5),
    .pin7(U31_pin1), .pin8(1'b0), .pin9(U53_pin4), .pin10(U53_pin4), .pin11(U30_pin15), .pin12(U30_pin16),
    .pin13(U30_pin17), .pin14(U30_pin18), .pin15(U51_pin11), .pin16(1'b1));
  LED A__0 (.in(U7_pin9));
  LED A__1 (.in(U7_pin8));
  LED CF (.in(U47_p14));
  LED ZF (.in(U47_p15));
  _74173 U19 (
    .pin1(1'b0), .pin2(1'b0), .pin3(U47_p14), .pin4(U47_p15), .pin7(U31_pin1), .pin8(1'b0), .pin9(U53_pin6),
    .pin10(U53_pin6), .pin11(notconnected_39_out), .pin12(notconnected_40_out), .pin13(U23_pin6),
    .pin14(U19_pin14), .pin15(U51_pin11), .pin16(1'b1));  // open: pin5, pin6
  _7402 U22 (
    .pin1(U23_pin1), .pin2(U22_pin2), .pin3(U22_pin3), .pin4(U23_pin2), .pin5(U22_pin5), .pin6(U22_pin6),
    .pin7(1'b0), .pin8(U22_pin8), .pin9(U22_pin9), .pin10(U23_pin9), .pin11(U22_pin11), .pin12(U22_pin12),
    .pin13(U23_pin10), .pin14(1'b1));
  LED A__2 (.in(U7_pin7));
  LED A__3 (.in(U7_pin6));
  LED B__0 (.in(U10_pin9));
  _74173 U9 (
    .pin1(1'b0), .pin2(1'b0), .pin3(U7_pin6), .pin4(U7_pin7), .pin5(U7_pin8), .pin6(U7_pin9),
    .pin7(U31_pin1), .pin8(1'b0), .pin9(U49_pin10), .pin10(U49_pin10), .pin11(U30_pin11), .pin12(U30_pin12),
    .pin13(U30_pin13), .pin14(U30_pin14), .pin15(U51_pin11), .pin16(1'b1));
  LED A__4 (.in(U7_pin5));
  LED A__5 (.in(U7_pin4));
  LED B__1 (.in(U10_pin8));
  LED B__2 (.in(U10_pin7));
  LED A__6 (.in(U7_pin3));
  LED A__7 (.in(U7_pin2));
  LED B__3 (.in(U10_pin6));
  LED B__4 (.in(U10_pin5));
  _74173 U12 (
    .pin1(1'b0), .pin2(1'b0), .pin3(U10_pin6), .pin4(U10_pin7), .pin5(U10_pin8), .pin6(U10_pin9),
    .pin7(U31_pin1), .pin8(1'b0), .pin9(U53_pin4), .pin10(U53_pin4), .pin11(U30_pin11), .pin12(U30_pin12),
    .pin13(U30_pin13), .pin14(U30_pin14), .pin15(U51_pin11), .pin16(1'b1));
  LED B__5 (.in(U10_pin4));
  LED B__6 (.in(U10_pin3));
  // _28c16 U45: pin names not known; wires that end beside it: U44_pin19, U44_pin16, U44_pin15, U44_pin12, U44_pin9, U44_pin6, U44_pin5, U44_pin2, U45_p9, U45_p10, U45_p11, 1'b0, 1'b1, U45_p14, U45_p15, 1'b1, 1'b0, DEC__HEX_p1, 1'b0, U45_p20, U45_p21, U45_p22
  LED SUM__0 (.in(U22_pin12));
  LED SUM__1 (.in(U22_pin11));
  LED SUM__2 (.in(U22_pin9));
  LED SUM__3 (.in(U22_pin8));
  LED SUM__4 (.in(U22_pin6));
  LED SUM__5 (.in(U22_pin5));
  LED SUM__6 (.in(U22_pin3));
  LED SUM__7 (.in(U22_pin2));
  LED B__7 (.in(U10_pin2));
  _74245 U17 (
    .pin1(1'b1), .pin2(U22_pin2), .pin3(U22_pin3), .pin4(U22_pin5), .pin5(U22_pin6), .pin6(U22_pin8),
    .pin7(U22_pin9), .pin8(U22_pin11), .pin9(U22_pin12), .pin10(1'b0), .pin11(U30_pin11), .pin12(U30_pin12),
    .pin13(U30_pin13), .pin14(U30_pin14), .pin15(U30_pin15), .pin16(U30_pin16), .pin17(U30_pin17),
    .pin18(U30_pin18), .pin19(U53_pin2), .pin20(1'b1));
  _7476 U37 (
    .pin1(MUX__CLK), .pin2(1'b1), .pin3(1'b1), .pin4(1'b1), .pin5(1'b1), .pin6(U45_p14), .pin7(1'b1),
    .pin8(1'b1), .pin9(1'b1), .pin10(U45_p15), .pin12(1'b1), .pin13(1'b0), .pin14(U45_p14), .pin16(1'b1));  // open: pin11, pin15
  // NotConnected on U10_pin19
  Seven_Seg #(.commonCathode("true"), .persistTime(4)) seven_seg_1 (
    .a(U45_p21), .b(U45_p22), .c(undriven), .d(undriven_2), .e(U45_p11), .f(U45_p10), .g(U45_p9),
    .dp(U45_p20), .common(U38_pin7));
  _74139 U38 (
    .pin1(1'b0), .pin2(U45_p14), .pin3(U45_p15), .pin4(U38_pin4), .pin5(U38_pin5), .pin6(U38_pin6),
    .pin7(U38_pin7), .pin8(1'b0), .pin13(U38_pin13), .pin14(U38_pin14), .pin15(U38_pin15), .pin16(1'b1));  // open: pin9, pin10, pin11, pin12
  Seven_Seg #(.commonCathode("true"), .persistTime(4)) seven_seg_2 (
    .a(U45_p21), .b(U45_p22), .c(undriven), .d(undriven_2), .e(U45_p11), .f(U45_p10), .g(U45_p9),
    .dp(U45_p20), .common(U38_pin6));
  Seven_Seg #(.commonCathode("true"), .persistTime(4)) seven_seg_3 (
    .a(U45_p21), .b(U45_p22), .c(undriven), .d(undriven_2), .e(U45_p11), .f(U45_p10), .g(U45_p9),
    .dp(U45_p20), .common(U38_pin5));
  _74283 U20 (
    .pin1(U22_pin5), .pin2(U20_pin2), .pin3(U7_pin4), .pin4(U22_pin6), .pin5(U7_pin5), .pin6(U20_pin6),
    .pin7(U20_pin7), .pin8(1'b0), .pin9(U19_pin14), .pin10(U22_pin2), .pin11(U20_pin11), .pin12(U7_pin2),
    .pin13(U22_pin3), .pin14(U7_pin3), .pin15(U20_pin15), .pin16(1'b1));
  _74283 U21 (
    .pin1(U22_pin11), .pin2(U21_pin2), .pin3(U7_pin8), .pin4(U22_pin12), .pin5(U7_pin9), .pin6(U21_pin6),
    .pin7(U52_p21), .pin8(1'b0), .pin9(U20_pin7), .pin10(U22_pin8), .pin11(U21_pin11), .pin12(U7_pin6),
    .pin13(U22_pin9), .pin14(U7_pin7), .pin15(U21_pin15), .pin16(1'b1));
  // NotConnected on U38_pin15
  // NotConnected on U38_pin14
  // NotConnected on U38_pin13
  Seven_Seg #(.commonCathode("true"), .persistTime(4)) seven_seg_4 (
    .a(U45_p21), .b(U45_p22), .c(undriven), .d(undriven_2), .e(U45_p11), .f(U45_p10), .g(U45_p9),
    .dp(U45_p20), .common(U38_pin4));
  _7486 U16 (
    .pin1(U10_pin4), .pin2(U52_p21), .pin3(U20_pin2), .pin4(U10_pin5), .pin5(U52_p21), .pin6(U20_pin6),
    .pin7(1'b0), .pin8(U20_pin11), .pin9(U10_pin2), .pin10(U52_p21), .pin11(U20_pin15), .pin12(U10_pin3),
    .pin13(U52_p21), .pin14(1'b1));
  _7486 U18 (
    .pin1(U10_pin8), .pin2(U52_p21), .pin3(U21_pin2), .pin4(U10_pin9), .pin5(U52_p21), .pin6(U21_pin6),
    .pin7(1'b0), .pin8(U21_pin11), .pin9(U10_pin6), .pin10(U52_p21), .pin11(U21_pin15), .pin12(U10_pin7),
    .pin13(U52_p21), .pin14(1'b1));

  // Notes on the sheet:
  //   MUX__CLK: Hz: 500
  //   RO\_hat
  //   PROG
  //   RAM\_CLK
  //   RI
  //   CLR\_hat
  //   CLR
  //   CLK\_hat
  //   CF
  //   ZF
  //   IR\_4
  //   IR\_5
  //   IR\_6
  //   IR\_7
  //   IREG\_BUS\_0
  //   IREG\_BUS\_1
  //   IREG\_BUS\_2
  //   IREG\_BUS\_3
  //   IREG\_BUS\_4
  //   IREG\_BUS\_5
  //   IREG\_BUS\_6
  //   IREG\_BUS\_7
  //   IREG\_CLK
  //   Instruction Register
  //   Control Logic
  //   HLT
  //   Random Access Memory
  //   Memory Address Register
  //   Clock
  //   IREG\_CLR
  //   II\_hat
  //   IO\_hat
  //   MI\_hat
  //   AI\_hat
  //   AO\_hat
  //   EO\_hat
  //   SU
  //   BI\_hat
  //   OI
  //   CE
  //   CO\_hat
  //   J\_hat
  //   FI\_hat
  //   A0
  //   A1
  //   A2
  //   A3
  //   RAM\_BUS\_7
  //   RAM\_BUS\_6
  //   RAM\_BUS\_5
  //   RAM\_BUS\_4
  //   RAM\_BUS\_3
  //   RAM\_BUS\_2
  //   RAM\_BUS\_1
  //   RAM\_BUS\_0
  //   MAR\_CLR
  //   MAR\_CLK
  //   MAR\_BUS\_0
  //   MAR\_BUS\_1
  //   MAR\_BUS\_2
  //   MAR\_BUS\_3
  //   CLK
  //   BUS
  //   OUTREG\_CLK
  //   OUTREG\_CLR\_hat
  //   AREG\_BUS\_0
  //   AREG\_BUS\_1
  //   AREG\_BUS\_2
  //   AREG\_BUS\_3
  //   AREG\_BUS\_4
  //   AREG\_BUS\_5
  //   AREG\_BUS\_6
  //   AREG\_BUS\_7
  //   ALU\_BUS\_0
  //   ALU\_BUS\_1
  //   ALU\_BUS\_2
  //   ALU\_BUS\_3
  //   ALU\_BUS\_4
  //   ALU\_BUS\_5
  //   ALU\_BUS\_6
  //   ALU\_BUS\_7
  //   ALU\_CLK
  //   ALU\_CLR
  //   OUTREG\_BUS\_0
  //   OUTREG\_BUS\_1
  //   OUTREG\_BUS\_2
  //   OUTREG\_BUS\_3
  //   OUTREG\_BUS\_4
  //   OUTREG\_BUS\_5
  //   OUTREG\_BUS\_6
  //   OUTREG\_BUS\_7
  //   Program Counter
  //   BREG\_BUS\_0
  //   BREG\_BUS\_1
  //   BREG\_BUS\_2
  //   BREG\_BUS\_3
  //   BREG\_BUS\_4
  //   BREG\_BUS\_5
  //   BREG\_BUS\_6
  //   BREG\_BUS\_7
  //   A Register
  //   Flags register
  //   B Register
  //   Output Register
  //   PC\_CLR\_hat
  //   PC\_CLK
  //   PC\_BUS\_0
  //   PC\_BUS\_1
  //   PC\_BUS\_2
  //   PC\_BUS\_3
  //   A\_0
  //   A\_1
  //   A\_2
  //   A\_3
  //   A\_4
  //   A\_5
  //   A\_6
  //   A\_7
  //   AREG\_CLK
  //   AREG\_CLR
  //   BREG\_CLK
  //   BREG\_CLR
  //   BO\_hat
  //   B\_0
  //   B\_1
  //   B\_2
  //   B\_3
  //   B\_4
  //   B\_5
  //   B\_6
  //   B\_7
  //   ALU
  //   contents of U52 (hex, n*v repeats v):
  //   4,8,6*0,4,8,6*0,4,8,0,20,81,0,0,0,4,8,0,20,c1,0,0,0,4,8,6*0,4,8,6*0,4,8,2,5*0,4,8,6*0,4,8,6*0,
  //   4,8,2,5*0,4,8,2,5*0,4,8,20,81,4*0,4,8,20,c1,4*0,4,8,20,81,4*0,4,8,10,5*0,4,8,6*0,4,8,6*0,4,
  //   8,6*0,4,8,0,20,81,0,0,0,4,8,0,20,c1,0,0,0,4,8,6*0,4,8,6*0,4,8,2,5*0,4,8,6*0,4,8,6*0,4,8,2,5*0,
  //   4,8,2,5*0,4,8,20,81,4*0,4,8,20,c1,4*0,4,8,20,81,4*0,4,8,10,5*0,4,8,6*0,4,8,6*0,4,8,6*0,4,8,
  //   0,20,81,0,0,0,4,8,0,20,c1,0,0,0,4,8,6*0,4,8,6*0,4,8,2,5*0,4,8,2,5*0,4,8,6*0,4,8,6*0,4,8,2,5*0,
  //   4,8,20,81,4*0,4,8,20,c1,4*0,4,8,20,81,4*0,4,8,10,5*0,4,8,6*0,4,8,6*0,4,8,6*0,4,8,0,20,81,0,
  //   0,0,4,8,0,20,c1,0,0,0,4,8,6*0,4,8,6*0,4,8,2,5*0,4,8,2,5*0,4,8,6*0,4,8,6*0,4,8,2,5*0,4,8,20,
  //   81,4*0,4,8,20,c1,4*0,4,8,20,81,4*0,4,8,10,5*0,4,8,6*0,4,8,6*0,4,8,6*0,4,8,0,20,81,0,0,0,4,8,
  //   0,20,c1,0,0,0,4,8,6*0,4,8,6*0,4,8,2,5*0,4,8,6*0,4,8,2,5*0,4,8,2,5*0,4,8,6*0,4,8,20,81,4*0,4,
  //   8,20,c1,4*0,4,8,20,81,4*0,4,8,10,5*0,4,8,6*0,4,8,6*0,4,8,6*0,4,8,0,20,81,0,0,0,4,8,0,20,c1,
  //   0,0,0,4,8,6*0,4,8,6*0,4,8,2,5*0,4,8,6*0,4,8,2,5*0,4,8,2,5*0,4,8,6*0,4,8,20,81,4*0,4,8,20,c1,
  //   4*0,4,8,20,81,4*0,4,8,10,5*0,4,8,6*0,4,8,6*0,4,8,6*0,4,8,0,20,81,0,0,0,4,8,0,20,c1,0,0,0,4,
  //   8,6*0,4,8,6*0,4,8,2,5*0,4,8,2,5*0,4,8,2,5*0,4,8,6*0,4,8,6*0,4,8,20,81,4*0,4,8,20,c1,4*0,4,8,
  //   20,81,4*0,4,8,10,5*0,4,8,6*0,4,8,6*0,4,8,6*0,4,8,0,20,81,0,0,0,4,8,0,20,c1,0,0,0,4,8,6*0,4,
  //   8,6*0,4,8,2,5*0,4,8,2,5*0,4,8,2,5*0,4,8,6*0,4,8,6*0,4,8,20,81,4*0,4,8,20,c1,4*0,4,8,20,81,4*0,
  //   4,8,10,5*0,4,8,6*0,4,8,6*0,4,8,6*0,4,8,0,20,81,0,0,0,4,8,0,20,c1,0,0,0,4,8,6*0,4,8,6*0,4,8,
  //   2,5*0,4,8,6*0,4,8,6*0,4,8,2,5*0,4,8,2,5*0,4,8,20,81,4*0,4,8,20,c1,4*0,4,8,20,81,4*0,4,8,10,
  //   5*0,4,8,6*0,4,8,6*0,4,8,6*0,4,8,0,20,81,0,0,0,4,8,0,20,c1,0,0,0,4,8,6*0,4,8,6*0,4,8,2,5*0,4,
  //   8,6*0,4,8,6*0,4,8,2,5*0,4,8,2,5*0,4,8,20,81,4*0,4,8,20,c1,4*0,4,8,20,81,4*0,4,8,10,5*0,4,8,
  //   6*0,4,8,6*0,4,8,6*0,4,8,0,20,81,0,0,0,4,8,0,20,c1,0,0,0,4,8,6*0,4,8,6*0,4,8,2,5*0,4,8,2,5*0,
  //   4,8,6*0,4,8,6*0,4,8,2,5*0,4,8,20,81,4*0,4,8,20,c1,4*0,4,8,20,81,4*0,4,8,10,5*0,4,8,6*0,4,8,
  //   6*0,4,8,6*0,4,8,0,20,81,0,0,0,4,8,0,20,c1,0,0,0,4,8,6*0,4,8,6*0,4,8,2,5*0,4,8,2,5*0,4,8,6*0,
  //   4,8,6*0,4,8,2,5*0,4,8,20,81,4*0,4,8,20,c1,4*0,4,8,20,81,4*0,4,8,10,5*0,4,8,6*0,4,8,6*0,4,8,
  //   6*0,4,8,0,20,81,0,0,0,4,8,0,20,c1,0,0,0,4,8,6*0,4,8,6*0,4,8,2,5*0,4,8,6*0,4,8,2,5*0,4,8,2,5*0,
  //   4,8,6*0,4,8,20,81,4*0,4,8,20,c1,4*0,4,8,20,81,4*0,4,8,10,5*0,4,8,6*0,4,8,6*0,4,8,6*0,4,8,0,
  //   20,81,0,0,0,4,8,0,20,c1,0,0,0,4,8,6*0,4,8,6*0,4,8,2,5*0,4,8,6*0,4,8,2,5*0,4,8,2,5*0,4,8,6*0,
  //   4,8,20,81,4*0,4,8,20,c1,4*0,4,8,20,81,4*0,4,8,10,5*0,4,8,6*0,4,8,6*0,4,8,6*0,4,8,0,20,81,0,
  //   0,0,4,8,0,20,c1,0,0,0,4,8,6*0,4,8,6*0,4,8,2,5*0,4,8,2,5*0,4,8,2,5*0,4,8,6*0,4,8,6*0,4,8,20,
  //   81,4*0,4,8,20,c1,4*0,4,8,20,81,4*0,4,8,10,5*0,4,8,6*0,4,8,6*0,4,8,6*0,4,8,0,20,81,0,0,0,4,8,
  //   0,20,c1,0,0,0,4,8,6*0,4,8,6*0,4,8,2,5*0,4,8,2,5*0,4,8,2,5*0,4,8,6*0,4,8,6*0,4,8,20,81,4*0,4,
  //   8,20,c1,4*0,4,8,20,81,4*0,4,8,10,5*0,4,8,6*0
  //   contents of U45 (hex, n*v repeats v):
  //   7e,30,6d,79,33,5b,5f,70,7f,7b,77,1f,4e,3d,4f,47,7e,30,6d,79,33 ,5b,5f,70,7f,7b,77,1f,4e,3d,
  //   4f,47,7e,30,6d,79,33,5b,5f,70,7f,7b ,77,1f,4e,3d,4f,47,7e,30,6d,79,33,5b,5f,70,7f,7b,77,1f,
  //   4e,3d,4f ,47,7e,30,6d,79,33,5b,5f,70,7f,7b,77,1f,4e,3d,4f,47,7e,30,6d,79 ,33,5b,5f,70,7f,7b,
  //   77,1f,4e,3d,4f,47,7e,30,6d,79,33,5b,5f,70,7f ,7b,77,1f,4e,3d,4f,47,7e,30,6d,79,33,5b,5f,70,
  //   7f,7b,77,1f,4e,3d ,4f,47,7e,30,6d,79,33,5b,5f,70,7f,7b,77,1f,4e,3d,4f,47,7e,30,6d ,79,33,5b,
  //   5f,70,7f,7b,77,1f,4e,3d,4f,47,7e,30,6d,79,33,5b,5f,70 ,7f,7b,77,1f,4e,3d,4f,47,7e,30,6d,79,
  //   33,5b,5f,70,7f,7b,77,1f,4e ,3d,4f,47,7e,30,6d,79,33,5b,5f,70,7f,7b,77,1f,4e,3d,4f,47,7e,30 ,
  //   6d,79,33,5b,5f,70,7f,7b,77,1f,4e,3d,4f,47,7e,30,6d,79,33,5b,5f ,70,7f,7b,77,1f,4e,3d,4f,47,
  //   7e,30,6d,79,33,5b,5f,70,7f,7b,77,1f ,4e,3d,4f,47,16*0,16*30,16*6d,16*79,16*33,16*5b,16*5f,16*70,
  //   16*7f ,16*7b,16*77,16*1f,16*4e,16*3d,16*4f,16*47,512*0,7e,30,6d,79,33 ,5b,5f,70,7f,7b,7e,30,
  //   6d,79,33,5b,5f,70,7f,7b,7e,30,6d,79,33,5b ,5f,70,7f,7b,7e,30,6d,79,33,5b,5f,70,7f,7b,7e,30,
  //   6d,79,33,5b,5f ,70,7f,7b,7e,30,6d,79,33,5b,5f,70,7f,7b,7e,30,6d,79,33,5b,5f,70 ,7f,7b,7e,30,
  //   6d,79,33,5b,5f,70,7f,7b,7e,30,6d,79,33,5b,5f,70,7f ,7b,7e,30,6d,79,33,5b,5f,70,7f,7b,7e,30,
  //   6d,79,33,5b,5f,70,7f,7b ,7e,30,6d,79,33,5b,5f,70,7f,7b,7e,30,6d,79,33,5b,5f,70,7f,7b,7e ,30,
  //   6d,79,33,5b,5f,70,7f,7b,7e,30,6d,79,33,5b,5f,70,7f,7b,7e,30 ,6d,79,33,5b,5f,70,7f,7b,7e,30,
  //   6d,79,33,5b,5f,70,7f,7b,7e,30,6d ,79,33,5b,5f,70,7f,7b,7e,30,6d,79,33,5b,5f,70,7f,7b,7e,30,
  //   6d,79 ,33,5b,5f,70,7f,7b,7e,30,6d,79,33,5b,5f,70,7f,7b,7e,30,6d,79,33 ,5b,5f,70,7f,7b,7e,30,
  //   6d,79,33,5b,5f,70,7f,7b,7e,30,6d,79,33,5b ,5f,70,7f,7b,7e,30,6d,79,33,5b,5f,70,7f,7b,7e,30,
  //   6d,79,33,5b,10*0 ,10*30,10*6d,10*79,10*33,10*5b,10*5f,10*70,10*7f,10*7b,10*7e,10*30 ,10*6d,
  //   10*79,10*33,10*5b,10*5f,10*70,10*7f,10*7b,10*7e,10*30,10*6d ,10*79,10*33,6*5b,100*0,100*30,
  //   56*6d
  //   contents of U47 (hex, n*v repeats v):
  //   40,14,6*0,40,14,48,12,4*0,40,14,48,10,2,0,0,0,40,14,48,10,2,0,0,0,40,14,48,21,4*0,40,14,a,5*0,
  //   40,14,8,5*0,40,14,6*0,40,14,6*0,40,14,8,5*0,40,14,8,5*0,40,14,8,2,4*0,40,14,8,2,4*0,40,14,1,
  //   2,4*0,40,14,1,5*0,40,14,80,5*0,40,14,6*0,40,14,48,12,4*0,40,14,48,10,2,0,0,0,40,14,48,10,2,
  //   0,0,0,40,14,48,21,4*0,40,14,a,5*0,40,14,8,5*0,40,14,6*0,40,14,6*0,40,14,8,5*0,40,14,8,5*0,40,
  //   14,8,2,4*0,40,14,8,2,4*0,40,14,1,2,4*0,40,14,1,5*0,40,14,80,5*0,40,14,6*0,40,14,48,12,4*0,40,
  //   14,48,10,2,0,0,0,40,14,48,10,2,0,0,0,40,14,48,21,4*0,40,14,a,5*0,40,14,8,5*0,40,14,8,5*0,40,
  //   14,6*0,40,14,6*0,40,14,8,5*0,40,14,8,2,4*0,40,14,8,2,4*0,40,14,1,2,4*0,40,14,1,5*0,40,14,80,
  //   5*0,40,14,6*0,40,14,48,12,4*0,40,14,48,10,2,0,0,0,40,14,48,10,2,0,0,0,40,14,48,21,4*0,40,14,
  //   a,5*0,40,14,8,5*0,40,14,8,5*0,40,14,6*0,40,14,6*0,40,14,8,5*0,40,14,8,2,4*0,40,14,8,2,4*0,40,
  //   14,1,2,4*0,40,14,1,5*0,40,14,80,5*0,40,14,6*0,40,14,48,12,4*0,40,14,48,10,2,0,0,0,40,14,48,
  //   10,2,0,0,0,40,14,48,21,4*0,40,14,a,5*0,40,14,8,5*0,40,14,6*0,40,14,8,5*0,40,14,8,5*0,40,14,
  //   6*0,40,14,8,2,4*0,40,14,8,2,4*0,40,14,1,2,4*0,40,14,1,5*0,40,14,80,5*0,40,14,6*0,40,14,48,12,
  //   4*0,40,14,48,10,2,0,0,0,40,14,48,10,2,0,0,0,40,14,48,21,4*0,40,14,a,5*0,40,14,8,5*0,40,14,6*0,
  //   40,14,8,5*0,40,14,8,5*0,40,14,6*0,40,14,8,2,4*0,40,14,8,2,4*0,40,14,1,2,4*0,40,14,1,5*0,40,
  //   14,80,5*0,40,14,6*0,40,14,48,12,4*0,40,14,48,10,2,0,0,0,40,14,48,10,2,0,0,0,40,14,48,21,4*0,
  //   40,14,a,5*0,40,14,8,5*0,40,14,8,5*0,40,14,8,5*0,40,14,6*0,40,14,6*0,40,14,8,2,4*0,40,14,8,2,
  //   4*0,40,14,1,2,4*0,40,14,1,5*0,40,14,80,5*0,40,14,6*0,40,14,48,12,4*0,40,14,48,10,2,0,0,0,40,
  //   14,48,10,2,0,0,0,40,14,48,21,4*0,40,14,a,5*0,40,14,8,5*0,40,14,8,5*0,40,14,8,5*0,40,14,6*0,
  //   40,14,6*0,40,14,8,2,4*0,40,14,8,2,4*0,40,14,1,2,4*0,40,14,1,5*0,40,14,80,5*0,40,14,6*0,40,14,
  //   48,12,4*0,40,14,48,10,2,0,0,0,40,14,48,10,2,0,0,0,40,14,48,21,4*0,40,14,a,5*0,40,14,8,5*0,40,
  //   14,6*0,40,14,6*0,40,14,8,5*0,40,14,8,5*0,40,14,8,2,4*0,40,14,8,2,4*0,40,14,1,2,4*0,40,14,1,
  //   5*0,40,14,80,5*0,40,14,6*0,40,14,48,12,4*0,40,14,48,10,2,0,0,0,40,14,48,10,2,0,0,0,40,14,48,
  //   21,4*0,40,14,a,5*0,40,14,8,5*0,40,14,6*0,40,14,6*0,40,14,8,5*0,40,14,8,5*0,40,14,8,2,4*0,40,
  //   14,8,2,4*0,40,14,1,2,4*0,40,14,1,5*0,40,14,80,5*0,40,14,6*0,40,14,48,12,4*0,40,14,48,10,2,0,
  //   0,0,40,14,48,10,2,0,0,0,40,14,48,21,4*0,40,14,a,5*0,40,14,8,5*0,40,14,8,5*0,40,14,6*0,40,14,
  //   6*0,40,14,8,5*0,40,14,8,2,4*0,40,14,8,2,4*0,40,14,1,2,4*0,40,14,1,5*0,40,14,80,5*0,40,14,6*0,
  //   40,14,48,12,4*0,40,14,48,10,2,0,0,0,40,14,48,10,2,0,0,0,40,14,48,21,4*0,40,14,a,5*0,40,14,8,
  //   5*0,40,14,8,5*0,40,14,6*0,40,14,6*0,40,14,8,5*0,40,14,8,2,4*0,40,14,8,2,4*0,40,14,1,2,4*0,40,
  //   14,1,5*0,40,14,80,5*0,40,14,6*0,40,14,48,12,4*0,40,14,48,10,2,0,0,0,40,14,48,10,2,0,0,0,40,
  //   14,48,21,4*0,40,14,a,5*0,40,14,8,5*0,40,14,6*0,40,14,8,5*0,40,14,8,5*0,40,14,6*0,40,14,8,2,
  //   4*0,40,14,8,2,4*0,40,14,1,2,4*0,40,14,1,5*0,40,14,80,5*0,40,14,6*0,40,14,48,12,4*0,40,14,48,
  //   10,2,0,0,0,40,14,48,10,2,0,0,0,40,14,48,21,4*0,40,14,a,5*0,40,14,8,5*0,40,14,6*0,40,14,8,5*0,
  //   40,14,8,5*0,40,14,6*0,40,14,8,2,4*0,40,14,8,2,4*0,40,14,1,2,4*0,40,14,1,5*0,40,14,80,5*0,40,
  //   14,6*0,40,14,48,12,4*0,40,14,48,10,2,0,0,0,40,14,48,10,2,0,0,0,40,14,48,21,4*0,40,14,a,5*0,
  //   40,14,8,5*0,40,14,8,5*0,40,14,8,5*0,40,14,6*0,40,14,6*0,40,14,8,2,4*0,40,14,8,2,4*0,40,14,1,
  //   2,4*0,40,14,1,5*0,40,14,80,5*0,40,14,6*0,40,14,48,12,4*0,40,14,48,10,2,0,0,0,40,14,48,10,2,
  //   0,0,0,40,14,48,21,4*0,40,14,a,5*0,40,14,8,5*0,40,14,8,5*0,40,14,8,5*0,40,14,6*0,40,14,6*0,40,
  //   14,8,2,4*0,40,14,8,2,4*0,40,14,1,2,4*0,40,14,1,5*0,40,14,80,5*0
endmodule
