// Digital circuit Control Logic.dig as structural Verilog
module Control_Logic (
  input  CF,
  input  ZF,
  input  IR__4,
  input  IR__5,
  input  IR__6,
  input  IR__7,
  input  CLK__hat,
  output CLR__hat,
  output CLR,
  output HLT,
  output MI__hat,
  output RI,
  output RO__hat,
  output IO__hat,
  output II__hat,
  output AI__hat,
  output AO__hat,
  output EO__hat,
  output SU,
  output BI__hat,
  output OI,
  output CE,
  output CO__hat,
  output J__hat,
  output FI__hat
);

  wire notconnected_1_out, notconnected_2_out, notconnected_3_out, notconnected_4_out, U47_p9, U47_p10,
       U47_p11, U47_p21, U48_pin1, U48_pin12, U48_pin13, U48_pin14, U49_pin3, U49_pin5, U50_pin10, U50_pin11,
       U50_pin12, U50_pin13, U50_pin14, U50_pin15, U51_pin1, U51_pin9, U52_p9, U52_p10, U52_p11, U52_p20,
       U52_p22, U53_pin9;

  // NotConnected on notconnected_1_out
  // NotConnected on notconnected_2_out
  // NotConnected on notconnected_3_out
  // NotConnected on notconnected_4_out
  LED led_1 (.in(U50_pin11));
  LED led_2 (.in(U50_pin12));
  LED led_3 (.in(U50_pin13));
  LED led_4 (.in(U50_pin14));
  LED led_5 (.in(U50_pin15));
  _74161 U48 (
    .pin1(U48_pin1), .pin2(CLK__hat), .pin3(notconnected_1_out), .pin4(notconnected_2_out),
    .pin5(notconnected_3_out), .pin6(notconnected_4_out), .pin7(1'b1), .pin8(1'b0), .pin9(1'b1),
    .pin10(1'b1), .pin12(U48_pin12), .pin13(U48_pin13), .pin14(U48_pin14), .pin16(1'b1));  // open: pin11, pin15
  _74138 U50 (
    .pin1(U48_pin14), .pin2(U48_pin13), .pin3(U48_pin12), .pin4(1'b0), .pin5(1'b0), .pin6(1'b1), .pin8(1'b0),
    .pin10(U50_pin10), .pin11(U50_pin11), .pin12(U50_pin12), .pin13(U50_pin13), .pin14(U50_pin14),
    .pin15(U50_pin15), .pin16(1'b1));  // open: pin7, pin9
  _7400 U51 (
    .pin1(U51_pin1), .pin2(U51_pin1), .pin3(U48_pin1), .pin4(CLR__hat), .pin5(U50_pin10), .pin6(U51_pin1),
    .pin7(1'b0), .pin8(CLR__hat), .pin9(U51_pin9), .pin10(U51_pin9), .pin11(CLR), .pin12(CLR__hat),
    .pin13(CLR__hat), .pin14(1'b1));
  // SwitchDT RESET: pin names not known; wires that end beside it: U51_pin9, 1'b1, 1'b0
  LED led_6 (.in(U48_pin14));
  LED led_7 (.in(U48_pin13));
  LED led_8 (.in(U48_pin12));
  LED led_9 (.in(HLT));
  LED led_10 (.in(RI));
  LED led_11 (.in(U47_p21));
  // _28c16 U47: pin names not known; wires that end beside it: 1'b1, IR__7, IR__6, IR__5, IR__4, U48_pin12, U48_pin13, U48_pin14, U47_p9, U47_p10, U47_p11, 1'b0, 1'b1, CF, ZF, 1'b1, 1'b0, 1'b0, 1'b0, HLT, U47_p21, RI
  // _28c16 U52: pin names not known; wires that end beside it: 1'b1, IR__7, IR__6, IR__5, IR__4, U48_pin12, U48_pin13, U48_pin14, U52_p9, U52_p10, U52_p11, 1'b0, 1'b1, CF, ZF, 1'b1, 1'b0, 1'b0, 1'b0, U52_p20, SU, U52_p22
  LED led_12 (.in(U49_pin3));
  LED led_13 (.in(U49_pin5));
  LED led_14 (.in(U47_p10));
  LED led_15 (.in(U47_p11));
  LED led_16 (.in(U47_p9));
  LED led_17 (.in(U52_p20));
  LED led_18 (.in(U52_p22));
  LED led_19 (.in(SU));
  LED led_20 (.in(OI));
  LED led_21 (.in(CE));
  LED led_22 (.in(U52_p10));
  LED led_23 (.in(U52_p11));
  LED led_24 (.in(U52_p9));
  _7404 U49 (
    .pin1(U47_p21), .pin2(MI__hat), .pin3(U49_pin3), .pin4(RO__hat), .pin5(U49_pin5), .pin6(IO__hat),
    .pin7(1'b0), .pin8(AO__hat), .pin9(U47_p9), .pin10(AI__hat), .pin11(U47_p10), .pin12(II__hat),
    .pin13(U47_p11), .pin14(1'b1));
  _7404 U53 (
    .pin1(U52_p20), .pin2(EO__hat), .pin3(U52_p22), .pin4(BI__hat), .pin5(U52_p9), .pin6(FI__hat),
    .pin7(1'b0), .pin9(U53_pin9), .pin10(J__hat), .pin11(U52_p10), .pin12(CO__hat), .pin13(U52_p11),
    .pin14(1'b1));  // open: pin8
  // NotConnected on U53_pin9

  // Notes on the sheet:
  //   contents of U52 (hex, n*v repeats v):
  //   4,8,6*0,4,8,6*0,4,8,0,20,81,0,0,0,4,8,0,20,c1,0,0,0,4,8,6*0,4 ,8,6*0,4,8,2,5*0,4,8,6*0,4,8,
  //   6*0,4,8,6*0,4,8,6*0,4,8,6*0,4,8,6*0 ,4,8,6*0,4,8,10,5*0,4,8,6*0,4,8,6*0,4,8,6*0,4,8,0,20,81,
  //   0,0,0 ,4,8,0,20,c1,0,0,0,4,8,6*0,4,8,6*0,4,8,2,5*0,4,8,6*0,4,8,6*0,4 ,8,6*0,4,8,6*0,4,8,6*0,
  //   4,8,6*0,4,8,6*0,4,8,10,5*0,4,8,6*0,4,8 ,6*0,4,8,6*0,4,8,0,20,81,0,0,0,4,8,0,20,c1,0,0,0,4,8,
  //   6*0,4,8,6*0 ,4,8,2,5*0,4,8,2,5*0,4,8,6*0,4,8,6*0,4,8,6*0,4,8,6*0,4,8,6*0,4 ,8,6*0,4,8,10,5*0,
  //   4,8,6*0,4,8,6*0,4,8,6*0,4,8,0,20,81,0,0,0,4 ,8,0,20,c1,0,0,0,4,8,6*0,4,8,6*0,4,8,2,5*0,4,8,
  //   2,5*0,4,8,6*0,4 ,8,6*0,4,8,6*0,4,8,6*0,4,8,6*0,4,8,6*0,4,8,10,5*0,4,8,6*0,4,8 ,6*0,4,8,6*0,
  //   4,8,0,20,81,0,0,0,4,8,0,20,c1,0,0,0,4,8,6*0,4,8,6*0 ,4,8,2,5*0,4,8,6*0,4,8,2,5*0,4,8,6*0,4,
  //   8,6*0,4,8,6*0,4,8,6*0,4 ,8,6*0,4,8,10,5*0,4,8,6*0,4,8,6*0,4,8,6*0,4,8,0,20,81,0,0,0,4 ,8,0,
  //   20,c1,0,0,0,4,8,6*0,4,8,6*0,4,8,2,5*0,4,8,6*0,4,8,2,5*0,4 ,8,6*0,4,8,6*0,4,8,6*0,4,8,6*0,4,
  //   8,6*0,4,8,10,5*0,4,8,6*0,4,8 ,6*0,4,8,6*0,4,8,0,20,81,0,0,0,4,8,0,20,c1,0,0,0,4,8,6*0,4,8,6*0 ,
  //   4,8,2,5*0,4,8,2,5*0,4,8,2,5*0,4,8,6*0,4,8,6*0,4,8,6*0,4,8,6*0 ,4,8,6*0,4,8,10,5*0,4,8,6*0,4,
  //   8,6*0,4,8,6*0,4,8,0,20,81,0,0,0 ,4,8,0,20,c1,0,0,0,4,8,6*0,4,8,6*0,4,8,2,5*0,4,8,2,5*0,4,8,
  //   2,5*0 ,4,8,6*0,4,8,6*0,4,8,6*0,4,8,6*0,4,8,6*0,4,8,10,5*0,4,8,6*0,4 ,8,6*0,4,8,6*0,4,8,0,20,
  //   81,0,0,0,4,8,0,20,c1,0,0,0,4,8,6*0,4,8 ,6*0,4,8,2,5*0,4,8,6*0,4,8,6*0,4,8,6*0,4,8,6*0,4,8,6*0,
  //   4,8,6*0 ,4,8,6*0,4,8,10,5*0,4,8,6*0,4,8,6*0,4,8,6*0,4,8,0,20,81,0,0,0 ,4,8,0,20,c1,0,0,0,4,
  //   8,6*0,4,8,6*0,4,8,2,5*0,4,8,6*0,4,8,6*0,4 ,8,6*0,4,8,6*0,4,8,6*0,4,8,6*0,4,8,6*0,4,8,10,5*0,
  //   4,8,6*0,4,8 ,6*0,4,8,6*0,4,8,0,20,81,0,0,0,4,8,0,20,c1,0,0,0,4,8,6*0,4,8,6*0 ,4,8,2,5*0,4,8,
  //   2,5*0,4,8,6*0,4,8,6*0,4,8,6*0,4,8,6*0,4,8,6*0,4 ,8,6*0,4,8,10,5*0,4,8,6*0,4,8,6*0,4,8,6*0,4,
  //   8,0,20,81,0,0,0,4 ,8,0,20,c1,0,0,0,4,8,6*0,4,8,6*0,4,8,2,5*0,4,8,2,5*0,4,8,6*0,4 ,8,6*0,4,8,
  //   6*0,4,8,6*0,4,8,6*0,4,8,6*0,4,8,10,5*0,4,8,6*0,4,8 ,6*0,4,8,6*0,4,8,0,20,81,0,0,0,4,8,0,20,
  //   c1,0,0,0,4,8,6*0,4,8,6*0 ,4,8,2,5*0,4,8,6*0,4,8,2,5*0,4,8,6*0,4,8,6*0,4,8,6*0,4,8,6*0,4 ,8,
  //   6*0,4,8,10,5*0,4,8,6*0,4,8,6*0,4,8,6*0,4,8,0,20,81,0,0,0,4 ,8,0,20,c1,0,0,0,4,8,6*0,4,8,6*0,
  //   4,8,2,5*0,4,8,6*0,4,8,2,5*0,4 ,8,6*0,4,8,6*0,4,8,6*0,4,8,6*0,4,8,6*0,4,8,10,5*0,4,8,6*0,4,8 ,
  //   6*0,4,8,6*0,4,8,0,20,81,0,0,0,4,8,0,20,c1,0,0,0,4,8,6*0,4,8,6*0 ,4,8,2,5*0,4,8,2,5*0,4,8,2,
  //   5*0,4,8,6*0,4,8,6*0,4,8,6*0,4,8,6*0 ,4,8,6*0,4,8,10,5*0,4,8,6*0,4,8,6*0,4,8,6*0,4,8,0,20,81,
  //   0,0,0 ,4,8,0,20,c1,0,0,0,4,8,6*0,4,8,6*0,4,8,2,5*0,4,8,2,5*0,4,8,2,5*0 ,4,8,6*0,4,8,6*0,4,8,
  //   6*0,4,8,6*0,4,8,6*0,4,8,10,5*0,4,8
  //   contents of U47 (hex, n*v repeats v):
  //   40,14,6*0,40,14,48,12,4*0,40,14,48,10,2,0,0,0,40,14,48,10,2,0,0,0 ,40,14,48,21,4*0,40,14,a,
  //   5*0,40,14,8,5*0,40,14,6*0,40,14,6*0,40 ,14,6*0,40,14,6*0,40,14,6*0,40,14,6*0,40,14,6*0,40,14,
  //   1,5*0,40 ,14,80,5*0,40,14,6*0,40,14,48,12,4*0,40,14,48,10,2,0,0,0,40,14 ,48,10,2,0,0,0,40,14,
  //   48,21,4*0,40,14,a,5*0,40,14,8,5*0,40,14,6*0 ,40,14,6*0,40,14,6*0,40,14,6*0,40,14,6*0,40,14,
  //   6*0,40,14,6*0,40 ,14,1,5*0,40,14,80,5*0,40,14,6*0,40,14,48,12,4*0,40,14,48,10,2 ,0,0,0,40,14,
  //   48,10,2,0,0,0,40,14,48,21,4*0,40,14,a,5*0,40,14,8 ,5*0,40,14,8,5*0,40,14,6*0,40,14,6*0,40,14,
  //   6*0,40,14,6*0,40,14 ,6*0,40,14,6*0,40,14,1,5*0,40,14,80,5*0,40,14,6*0,40,14,48,12 ,4*0,40,14,
  //   48,10,2,0,0,0,40,14,48,10,2,0,0,0,40,14,48,21,4*0,40 ,14,a,5*0,40,14,8,5*0,40,14,8,5*0,40,14,
  //   6*0,40,14,6*0,40,14,6*0 ,40,14,6*0,40,14,6*0,40,14,6*0,40,14,1,5*0,40,14,80,5*0,40,14 ,6*0,
  //   40,14,48,12,4*0,40,14,48,10,2,0,0,0,40,14,48,10,2,0,0,0,40 ,14,48,21,4*0,40,14,a,5*0,40,14,
  //   8,5*0,40,14,6*0,40,14,8,5*0,40 ,14,6*0,40,14,6*0,40,14,6*0,40,14,6*0,40,14,6*0,40,14,1,5*0,
  //   40 ,14,80,5*0,40,14,6*0,40,14,48,12,4*0,40,14,48,10,2,0,0,0,40,14 ,48,10,2,0,0,0,40,14,48,21,
  //   4*0,40,14,a,5*0,40,14,8,5*0,40,14,6*0 ,40,14,8,5*0,40,14,6*0,40,14,6*0,40,14,6*0,40,14,6*0,
  //   40,14,6*0 ,40,14,1,5*0,40,14,80,5*0,40,14,6*0,40,14,48,12,4*0,40,14,48,10 ,2,0,0,0,40,14,48,
  //   10,2,0,0,0,40,14,48,21,4*0,40,14,a,5*0,40,14 ,8,5*0,40,14,8,5*0,40,14,8,5*0,40,14,6*0,40,14,
  //   6*0,40,14,6*0,40 ,14,6*0,40,14,6*0,40,14,1,5*0,40,14,80,5*0,40,14,6*0,40,14,48 ,12,4*0,40,14,
  //   48,10,2,0,0,0,40,14,48,10,2,0,0,0,40,14,48,21,4*0 ,40,14,a,5*0,40,14,8,5*0,40,14,8,5*0,40,14,
  //   8,5*0,40,14,6*0,40 ,14,6*0,40,14,6*0,40,14,6*0,40,14,6*0,40,14,1,5*0,40,14,80,5*0 ,40,14,6*0,
  //   40,14,48,12,4*0,40,14,48,10,2,0,0,0,40,14,48,10,2,0,0,0 ,40,14,48,21,4*0,40,14,a,5*0,40,14,
  //   8,5*0,40,14,6*0,40,14,6*0,40 ,14,6*0,40,14,6*0,40,14,6*0,40,14,6*0,40,14,6*0,40,14,1,5*0,40 ,
  //   14,80,5*0,40,14,6*0,40,14,48,12,4*0,40,14,48,10,2,0,0,0,40,14 ,48,10,2,0,0,0,40,14,48,21,4*0,
  //   40,14,a,5*0,40,14,8,5*0,40,14,6*0 ,40,14,6*0,40,14,6*0,40,14,6*0,40,14,6*0,40,14,6*0,40,14,
  //   6*0,40 ,14,1,5*0,40,14,80,5*0,40,14,6*0,40,14,48,12,4*0,40,14,48,10,2 ,0,0,0,40,14,48,10,2,
  //   0,0,0,40,14,48,21,4*0,40,14,a,5*0,40,14,8 ,5*0,40,14,8,5*0,40,14,6*0,40,14,6*0,40,14,6*0,40,
  //   14,6*0,40,14 ,6*0,40,14,6*0,40,14,1,5*0,40,14,80,5*0,40,14,6*0,40,14,48,12 ,4*0,40,14,48,10,
  //   2,0,0,0,40,14,48,10,2,0,0,0,40,14,48,21,4*0,40 ,14,a,5*0,40,14,8,5*0,40,14,8,5*0,40,14,6*0,
  //   40,14,6*0,40,14,6*0 ,40,14,6*0,40,14,6*0,40,14,6*0,40,14,1,5*0,40,14,80,5*0,40,14 ,6*0,40,14,
  //   48,12,4*0,40,14,48,10,2,0,0,0,40,14,48,10,2,0,0,0,40 ,14,48,21,4*0,40,14,a,5*0,40,14,8,5*0,
  //   40,14,6*0,40,14,8,5*0,40 ,14,6*0,40,14,6*0,40,14,6*0,40,14,6*0,40,14,6*0,40,14,1,5*0,40 ,14,
  //   80,5*0,40,14,6*0,40,14,48,12,4*0,40,14,48,10,2,0,0,0,40,14 ,48,10,2,0,0,0,40,14,48,21,4*0,40,
  //   14,a,5*0,40,14,8,5*0,40,14,6*0 ,40,14,8,5*0,40,14,6*0,40,14,6*0,40,14,6*0,40,14,6*0,40,14,6*0 ,
  //   40,14,1,5*0,40,14,80,5*0,40,14,6*0,40,14,48,12,4*0,40,14,48,10 ,2,0,0,0,40,14,48,10,2,0,0,0,
  //   40,14,48,21,4*0,40,14,a,5*0,40,14 ,8,5*0,40,14,8,5*0,40,14,8,5*0,40,14,6*0,40,14,6*0,40,14,
  //   6*0,40 ,14,6*0,40,14,6*0,40,14,1,5*0,40,14,80,5*0,40,14,6*0,40,14,48 ,12,4*0,40,14,48,10,2,
  //   0,0,0,40,14,48,10,2,0,0,0,40,14,48,21,4*0 ,40,14,a,5*0,40,14,8,5*0,40,14,8,5*0,40,14,8,5*0,
  //   40,14,6*0,40 ,14,6*0,40,14,6*0,40,14,6*0,40,14,6*0,40,14,1,5*0,40,14,80
endmodule
