// Digital circuit Instruction Register.dig as structural Verilog
module Instruction_Register (
  input  BUS__0,
  input  BUS__1,
  input  BUS__2,
  input  BUS__3,
  input  BUS__4,
  input  BUS__5,
  input  BUS__6,
  input  BUS__7,
  input  I1__hat,
  input  CLR,
  input  I0__hat,
  input  CLK,
  output IR__4,
  output IR__5,
  output IR__6,
  output IR__7
);

  wire _74245_1_pin6, _74245_1_pin7, _74245_1_pin8, _74245_1_pin9;

  _74245 _74245_1 (
    .pin1(1'b1), .pin2(1'b0), .pin3(1'b0), .pin4(1'b0), .pin5(1'b0), .pin6(_74245_1_pin6),
    .pin7(_74245_1_pin7), .pin8(_74245_1_pin8), .pin9(_74245_1_pin9), .pin10(1'b0), .pin11(BUS__0),
    .pin12(BUS__1), .pin13(BUS__2), .pin14(BUS__3), .pin15(BUS__4), .pin16(BUS__5), .pin17(BUS__6),
    .pin18(BUS__7), .pin19(I0__hat), .pin20(1'b1));
  _74173 _74173_1 (
    .pin1(1'b0), .pin2(1'b0), .pin3(IR__7), .pin4(IR__6), .pin5(IR__5), .pin6(IR__4), .pin7(CLK),
    .pin8(1'b0), .pin9(I1__hat), .pin10(I1__hat), .pin11(BUS__4), .pin12(BUS__5), .pin13(BUS__6),
    .pin14(BUS__7), .pin15(CLR), .pin16(1'b1));
  LED led_1 (.in(_74245_1_pin9));
  LED led_2 (.in(_74245_1_pin8));
  LED led_3 (.in(_74245_1_pin7));
  LED led_4 (.in(_74245_1_pin6));
  LED led_5 (.in(IR__4));
  _74173 _74173_2 (
    .pin1(1'b0), .pin2(1'b0), .pin3(_74245_1_pin6), .pin4(_74245_1_pin7), .pin5(_74245_1_pin8),
    .pin6(_74245_1_pin9), .pin7(CLK), .pin8(1'b0), .pin9(I1__hat), .pin10(I1__hat), .pin11(BUS__0),
    .pin12(BUS__1), .pin13(BUS__2), .pin14(BUS__3), .pin15(CLR), .pin16(1'b1));
  LED led_6 (.in(IR__5));
  LED led_7 (.in(IR__6));
  LED led_8 (.in(IR__7));
endmodule
