// Digital circuit Memory Address Register.dig as structural Verilog
module Memory_Address_Register (
  input  CLR,
  input  CLK,
  input  MI__hat,
  input  BUS__0,
  input  BUS__1,
  input  BUS__2,
  input  BUS__3,
  output A3,
  output A2,
  output A1,
  output A0,
  output PROG
);

  wire not_1_out, U33_pin2, U33_pin3, U33_pin5, U33_pin6, U33_pin10, U33_pin11, U33_pin13, U33_pin14;

  not not_1 (not_1_out, PROG);
  // SwitchDT SW6: pin names not known; wires that end beside it: PROG, 1'b1, 1'b0
  LED led_1 (.in(not_1_out));
  LED led_2 (.in(PROG));
  LED led_3 (.in(A3));
  LED led_4 (.in(A2));
  _74157 U33 (
    .pin1(PROG), .pin2(U33_pin2), .pin3(U33_pin3), .pin4(A3), .pin5(U33_pin5), .pin6(U33_pin6), .pin7(A2),
    .pin8(1'b0), .pin9(A0), .pin10(U33_pin10), .pin11(U33_pin11), .pin12(A1), .pin13(U33_pin13),
    .pin14(U33_pin14), .pin15(1'b0), .pin16(1'b1));
  DipSwitch dipswitch_1 (.out(U33_pin2));
  DipSwitch dipswitch_2 (.out(U33_pin5));
  DipSwitch dipswitch_3 (.out(U33_pin11));
  LED led_5 (.in(A1));
  LED led_6 (.in(A0));
  DipSwitch SW5 (.out(U33_pin14));
  _74173 U34 (
    .pin1(1'b0), .pin2(1'b0), .pin3(U33_pin3), .pin4(U33_pin6), .pin5(U33_pin13), .pin6(U33_pin10),
    .pin7(CLK), .pin8(1'b0), .pin9(MI__hat), .pin10(MI__hat), .pin11(BUS__0), .pin12(BUS__1), .pin13(BUS__2),
    .pin14(BUS__3), .pin15(CLR), .pin16(1'b1));
endmodule
