// Digital circuit Output Register.dig as structural Verilog
module Output_Register (
  input  BUS__0,
  input  BUS__1,
  input  BUS__2,
  input  BUS__3,
  input  BUS__4,
  input  BUS__5,
  input  BUS__6,
  input  BUS__7,
  input  OI,
  input  CLK,
  input  CLR__hat,
  input  MUX__CLK
);

  wire notconnected_1_out, notconnected_2_out, SW7_p1, U38_pin4, U38_pin5, U38_pin6, U38_pin7, U38_pin13,
       U38_pin14, U38_pin15, U44_pin2, U44_pin5, U44_pin6, U44_pin9, U44_pin12, U44_pin15, U44_pin16,
       U44_pin19, U45_p9, U45_p10, U45_p11, U45_p14, U45_p15, U45_p20, U45_p21, U45_p22, U46_pin3, U46_pin9,
       U46_pin10, U46_pin12, U46_pin13, undriven, undriven_2;

  // NotConnected on notconnected_1_out
  // NotConnected on notconnected_2_out
  // SwitchDT SW7: pin names not known; wires that end beside it: SW7_p1, 1'b1, 1'b0
  _7408 U46 (
    .pin1(OI), .pin2(CLK), .pin3(U46_pin3), .pin4(notconnected_1_out), .pin5(notconnected_2_out),
    .pin7(1'b0), .pin9(U46_pin9), .pin10(U46_pin10), .pin12(U46_pin12), .pin13(U46_pin13), .pin14(1'b1));  // open: pin6, pin8, pin11
  // NotConnected on U46_pin13
  // NotConnected on U46_pin12
  // NotConnected on U46_pin10
  // NotConnected on U46_pin9
  _74273 U44 (
    .pin1(CLR__hat), .pin2(U44_pin2), .pin3(BUS__0), .pin4(BUS__1), .pin5(U44_pin5), .pin6(U44_pin6),
    .pin7(BUS__2), .pin8(BUS__3), .pin9(U44_pin9), .pin10(1'b0), .pin11(U46_pin3), .pin12(U44_pin12),
    .pin13(BUS__4), .pin14(BUS__5), .pin15(U44_pin15), .pin16(U44_pin16), .pin17(BUS__6), .pin18(BUS__7),
    .pin19(U44_pin19), .pin20(1'b1));
  // _28c16 U45: pin names not known; wires that end beside it: U44_pin19, U44_pin16, U44_pin15, U44_pin12, U44_pin9, U44_pin6, U44_pin5, U44_pin2, U45_p9, U45_p10, U45_p11, 1'b0, 1'b1, U45_p14, U45_p15, 1'b1, 1'b0, SW7_p1, 1'b0, U45_p20, U45_p21, U45_p22
  _7476 U37 (
    .pin1(MUX__CLK), .pin2(1'b1), .pin3(1'b1), .pin4(1'b1), .pin5(1'b1), .pin6(U45_p14), .pin7(1'b1),
    .pin8(1'b1), .pin9(1'b1), .pin10(U45_p15), .pin12(1'b1), .pin13(1'b0), .pin14(U45_p14), .pin16(1'b1));  // open: pin11, pin15
  Seven_Seg #(.commonCathode("true"), .persistTime(4)) seven_seg_1 (
    .a(U45_p21), .b(U45_p22), .c(undriven_2), .d(undriven), .e(U45_p11), .f(U45_p10), .g(U45_p9),
    .dp(U45_p20), .common(U38_pin7));
  _74139 U38 (
    .pin1(1'b0), .pin2(U45_p14), .pin3(U45_p15), .pin4(U38_pin4), .pin5(U38_pin5), .pin6(U38_pin6),
    .pin7(U38_pin7), .pin8(1'b0), .pin13(U38_pin13), .pin14(U38_pin14), .pin15(U38_pin15), .pin16(1'b1));  // open: pin9, pin10, pin11, pin12
  Seven_Seg #(.commonCathode("true"), .persistTime(4)) seven_seg_2 (
    .a(U45_p21), .b(U45_p22), .c(undriven_2), .d(undriven), .e(U45_p11), .f(U45_p10), .g(U45_p9),
    .dp(U45_p20), .common(U38_pin6));
  Seven_Seg #(.commonCathode("true"), .persistTime(4)) seven_seg_3 (
    .a(U45_p21), .b(U45_p22), .c(undriven_2), .d(undriven), .e(U45_p11), .f(U45_p10), .g(U45_p9),
    .dp(U45_p20), .common(U38_pin5));
  // NotConnected on U38_pin15
  // NotConnected on U38_pin14
  // NotConnected on U38_pin13
  Seven_Seg #(.commonCathode("true"), .persistTime(4)) seven_seg_4 (
    .a(U45_p21), .b(U45_p22), .c(undriven_2), .d(undriven), .e(U45_p11), .f(U45_p10), .g(U45_p9),
    .dp(U45_p20), .common(U38_pin4));

  // Notes on the sheet:
  //   MUX__CLK: Hz: 500
  //   contents of U45 (hex, n*v repeats v):
  //   7e,30,6d,79,33,5b,5f,70,7f,7b,77,1f,4e,3d,4f,47,7e,30,6d,79,33 ,5b,5f,70,7f,7b,77,1f,4e,3d,
  //   4f,47,7e,30,6d,79,33,5b,5f,70,7f,7b ,77,1f,4e,3d,4f,47,7e,30,6d,79,33,5b,5f,70,7f,7b,77,1f,
  //   4e,3d,4f ,47,7e,30,6d,79,33,5b,5f,70,7f,7b,77,1f,4e,3d,4f,47,7e,30,6d,79 ,33,5b,5f,70,7f,7b,
  //   77,1f,4e,3d,4f,47,7e,30,6d,79,33,5b,5f,70,7f ,7b,77,1f,4e,3d,4f,47,7e,30,6d,79,33,5b,5f,70,
  //   7f,7b,77,1f,4e,3d ,4f,47,7e,30,6d,79,33,5b,5f,70,7f,7b,77,1f,4e,3d,4f,47,7e,30,6d ,79,33,5b,
  //   5f,70,7f,7b,77,1f,4e,3d,4f,47,7e,30,6d,79,33,5b,5f,70 ,7f,7b,77,1f,4e,3d,4f,47,7e,30,6d,79,
  //   33,5b,5f,70,7f,7b,77,1f,4e ,3d,4f,47,7e,30,6d,79,33,5b,5f,70,7f,7b,77,1f,4e,3d,4f,47,7e,30 ,
  //   6d,79,33,5b,5f,70,7f,7b,77,1f,4e,3d,4f,47,7e,30,6d,79,33,5b,5f ,70,7f,7b,77,1f,4e,3d,4f,47,
  //   7e,30,6d,79,33,5b,5f,70,7f,7b,77,1f ,4e,3d,4f,47,16*0,16*30,16*6d,16*79,16*33,16*5b,16*5f,16*70,
  //   16*7f ,16*7b,16*77,16*1f,16*4e,16*3d,16*4f,16*47,512*0,7e,30,6d,79,33 ,5b,5f,70,7f,7b,7e,30,
  //   6d,79,33,5b,5f,70,7f,7b,7e,30,6d,79,33,5b ,5f,70,7f,7b,7e,30,6d,79,33,5b,5f,70,7f,7b,7e,30,
  //   6d,79,33,5b,5f ,70,7f,7b,7e,30,6d,79,33,5b,5f,70,7f,7b,7e,30,6d,79,33,5b,5f,70 ,7f,7b,7e,30,
  //   6d,79,33,5b,5f,70,7f,7b,7e,30,6d,79,33,5b,5f,70,7f ,7b,7e,30,6d,79,33,5b,5f,70,7f,7b,7e,30,
  //   6d,79,33,5b,5f,70,7f,7b ,7e,30,6d,79,33,5b,5f,70,7f,7b,7e,30,6d,79,33,5b,5f,70,7f,7b,7e ,30,
  //   6d,79,33,5b,5f,70,7f,7b,7e,30,6d,79,33,5b,5f,70,7f,7b,7e,30 ,6d,79,33,5b,5f,70,7f,7b,7e,30,
  //   6d,79,33,5b,5f,70,7f,7b,7e,30,6d ,79,33,5b,5f,70,7f,7b,7e,30,6d,79,33,5b,5f,70,7f,7b,7e,30,
  //   6d,79 ,33,5b,5f,70,7f,7b,7e,30,6d,79,33,5b,5f,70,7f,7b,7e,30,6d,79,33 ,5b,5f,70,7f,7b,7e,30,
  //   6d,79,33,5b,5f,70,7f,7b,7e,30,6d,79,33,5b ,5f,70,7f,7b,7e,30,6d,79,33,5b,5f,70,7f,7b,7e,30,
  //   6d,79,33,5b,10*0 ,10*30,10*6d,10*79,10*33,10*5b,10*5f,10*70,10*7f,10*7b,10*7e,10*30 ,10*6d,
  //   10*79,10*33,10*5b,10*5f,10*70,10*7f,10*7b,10*7e,10*30,10*6d ,10*79,10*33,6*5b,100*0,100*30,
  //   56*6d
endmodule
