// Digital circuit Program Counter.dig as structural Verilog
module Program_Counter (
  input  J__hat,
  input  CE,
  input  CLK,
  input  CLR__hat,
  input  CO__hat,
  output BUS__0,
  output BUS__1,
  output BUS__2,
  output BUS__3
);

  wire U36_pin11, U36_pin12, U36_pin13, U36_pin14;

  _74245 U36 (
    .pin1(1'b0), .pin6(BUS__3), .pin7(BUS__2), .pin8(BUS__1), .pin9(BUS__0), .pin10(1'b0), .pin11(U36_pin11),
    .pin12(U36_pin12), .pin13(U36_pin13), .pin14(U36_pin14), .pin19(CO__hat), .pin20(1'b1));  // open: pin2, pin3, pin4, pin5, pin15, pin16, pin17, pin18
  LED led_1 (.in(U36_pin14));
  LED led_2 (.in(U36_pin13));
  LED led_3 (.in(U36_pin12));
  LED led_4 (.in(U36_pin11));
  _74161 U35 (
    .pin1(CLR__hat), .pin2(CLK), .pin3(BUS__0), .pin4(BUS__1), .pin5(BUS__2), .pin6(BUS__3), .pin7(CE),
    .pin8(1'b0), .pin9(J__hat), .pin10(CE), .pin11(U36_pin14), .pin12(U36_pin13), .pin13(U36_pin12),
    .pin14(U36_pin11), .pin16(1'b1));  // open: pin15
endmodule
