// Digital circuit Random Access Memory.dig as structural Verilog
module Random_Access_Memory (
  input  RO__hat,
  input  PROG,
  input  CLK,
  input  RI,
  input  A0,
  input  A1,
  input  A2,
  input  A3,
  output BUS__5,
  output BUS__7,
  output BUS__6,
  output BUS__4,
  output BUS__1,
  output BUS__3,
  output BUS__2,
  output BUS__0
);

  wire dipswitch_5_out, dipswitch_6_out, dipswitch_7_out, SW3_out, SW4_p1, U24_pin4, U24_pin5, U24_pin6,
       U24_pin7, U24_pin9, U24_pin10, U24_pin11, U24_pin12, U25_pin4, U25_pin6, U25_pin10, U25_pin12,
       U26_pin2, U26_pin5, U26_pin11, U26_pin14, U28_pin2, U28_pin4, U28_pin6, U28_pin8, U28_pin11,
       U28_pin13, U29_pin1, U29_pin2, U29_pin3, U29_pin4, U29_pin5, U29_pin6, U29_pin9, U29_pin11, U29_pin12,
       U29_pin13, U31_pin4, U31_pin5, U31_pin9, U31_pin10, U31_pin12, U31_pin13, U32_pin2, U32_pin3,
       U32_pin5, U32_pin6, U32_pin10, U32_pin11, U32_pin12, U32_pin13;

  // SwitchDT SW4: pin names not known; wires that end beside it: SW4_p1, 1'b1, 1'b0
  _74157 U32 (
    .pin1(PROG), .pin2(U32_pin2), .pin3(U32_pin3), .pin5(U32_pin5), .pin6(U32_pin6), .pin8(1'b0),
    .pin10(U32_pin10), .pin11(U32_pin11), .pin12(U32_pin12), .pin13(U32_pin13), .pin14(SW4_p1), .pin15(1'b0),
    .pin16(1'b1));  // open: pin4, pin7, pin9
  // NotConnected on U32_pin2
  // NotConnected on U32_pin3
  _74189 U24 (
    .pin1(A0), .pin2(1'b0), .pin3(U32_pin12), .pin4(U24_pin4), .pin5(U24_pin5), .pin6(U24_pin6),
    .pin7(U24_pin7), .pin8(1'b0), .pin9(U24_pin9), .pin10(U24_pin10), .pin11(U24_pin11), .pin12(U24_pin12),
    .pin13(A3), .pin14(A2), .pin15(A1), .pin16(1'b1));
  // NotConnected on U32_pin5
  // NotConnected on U32_pin11
  // NotConnected on U32_pin10
  // NotConnected on U32_pin6
  _7400 U31 (
    .pin1(CLK), .pin2(RI), .pin3(U32_pin13), .pin4(U31_pin4), .pin5(U31_pin5), .pin7(1'b0), .pin9(U31_pin9),
    .pin10(U31_pin10), .pin12(U31_pin12), .pin13(U31_pin13), .pin14(1'b1));  // open: pin6, pin8, pin11
  _7404 U28 (
    .pin1(U24_pin5), .pin2(U28_pin2), .pin3(U24_pin7), .pin4(U28_pin4), .pin5(U24_pin9), .pin6(U28_pin6),
    .pin7(1'b0), .pin8(U28_pin8), .pin9(U24_pin11), .pin11(U28_pin11), .pin13(U28_pin13), .pin14(1'b1));  // open: pin10, pin12
  // NotConnected on U31_pin13
  // NotConnected on U31_pin12
  // NotConnected on U28_pin13
  // NotConnected on U31_pin10
  // NotConnected on U31_pin4
  // NotConnected on U31_pin5
  // NotConnected on U28_pin11
  // NotConnected on U31_pin9
  LED led_1 (.in(U28_pin2));
  LED led_2 (.in(U28_pin4));
  _7404 U29 (
    .pin1(U29_pin1), .pin2(U29_pin2), .pin3(U29_pin3), .pin4(U29_pin4), .pin5(U29_pin5), .pin6(U29_pin6),
    .pin7(1'b0), .pin9(U29_pin9), .pin11(U29_pin11), .pin12(U29_pin12), .pin13(U29_pin13), .pin14(1'b1));  // open: pin8, pin10
  LED led_3 (.in(U28_pin6));
  LED led_4 (.in(U28_pin8));
  // NotConnected on U29_pin11
  LED led_5 (.in(U29_pin12));
  LED led_6 (.in(U29_pin2));
  // NotConnected on U29_pin9
  LED led_7 (.in(U29_pin4));
  LED led_8 (.in(U29_pin6));
  _74189 U25 (
    .pin1(A0), .pin2(1'b0), .pin3(U32_pin12), .pin4(U25_pin4), .pin5(U29_pin5), .pin6(U25_pin6),
    .pin7(U29_pin3), .pin8(1'b0), .pin9(U29_pin1), .pin10(U25_pin10), .pin11(U29_pin13), .pin12(U25_pin12),
    .pin13(A3), .pin14(A2), .pin15(A1), .pin16(1'b1));
  _74245 U30 (
    .pin1(1'b1), .pin2(U28_pin2), .pin3(U28_pin4), .pin4(U28_pin6), .pin5(U28_pin8), .pin6(U29_pin12),
    .pin7(U29_pin2), .pin8(U29_pin4), .pin9(U29_pin6), .pin10(1'b0), .pin11(BUS__0), .pin12(BUS__1),
    .pin13(BUS__2), .pin14(BUS__3), .pin15(BUS__4), .pin16(BUS__5), .pin17(BUS__6), .pin18(BUS__7),
    .pin19(RO__hat), .pin20(1'b1));
  _74157 U26 (
    .pin1(PROG), .pin2(U26_pin2), .pin3(BUS__7), .pin4(U24_pin4), .pin5(U26_pin5), .pin6(BUS__6),
    .pin7(U24_pin6), .pin8(1'b0), .pin9(U24_pin12), .pin10(BUS__4), .pin11(U26_pin11), .pin12(U24_pin10),
    .pin13(BUS__5), .pin14(U26_pin14), .pin15(1'b0), .pin16(1'b1));
  DipSwitch dipswitch_1 (.out(U26_pin2));
  DipSwitch dipswitch_2 (.out(U26_pin5));
  DipSwitch dipswitch_3 (.out(U26_pin14));
  DipSwitch dipswitch_4 (.out(U26_pin11));
  DipSwitch dipswitch_5 (.out(dipswitch_5_out));
  DipSwitch dipswitch_6 (.out(dipswitch_6_out));
  DipSwitch dipswitch_7 (.out(dipswitch_7_out));
  DipSwitch SW3 (.out(SW3_out));
  _74157 U27 (
    .pin1(PROG), .pin2(dipswitch_5_out), .pin3(BUS__3), .pin4(U25_pin12), .pin5(dipswitch_6_out),
    .pin6(BUS__2), .pin7(U25_pin10), .pin8(1'b0), .pin9(U25_pin4), .pin10(BUS__0), .pin11(SW3_out),
    .pin12(U25_pin6), .pin13(BUS__1), .pin14(dipswitch_7_out), .pin15(1'b0), .pin16(1'b1));
endmodule
