// Digital circuit dig245.dig as structural Verilog
// A single 74245 from the standard library, one bit used: OE enabled, direction set so the enabled bank reads the unwired (floating) A side and drives B1, which is also driven by input T. Stock 0.31: burn on the B1 net about half the time. Patched: never, RESULT = T.
module dig245 (
  input  DIR,
  input  OE,
  input  T,
  output RESULT
);

  // _74245 _74245_1: pin names not known; wires that end beside it: DIR, 1'b0, 1'b1, OE, T

  assign RESULT = T;
endmodule
