// Digital circuit driver_pullup.dig as structural Verilog
// Silent wrong value: an enabled Driver (S=1) reads a floating 4-bit net and drives it onto a net with only a pull-up resistor. Stock: RESULT shows a random value every run, no error. Patched: RESULT is always 15 (pull-up wins).
module driver_pullup (
  input  [3:0] SD,
  input  SD2,
  input  S,
  output [3:0] RESULT
);

  wire [3:0] driver_1_out;

  assign driver_1_out = SD2 ? SD : 4'bz;  // Driver driver_1
  assign RESULT = S ? driver_1_out : 4'bz;  // Driver driver_2
  PullUp #(.Bits(4)) pullup_1 (.out(RESULT));
endmodule
