// Digital circuit driver_z2.dig as structural Verilog
// Minimal repro: an enabled Driver (S=1) whose input net is floating (its only output is a disabled Driver, so high-Z). Its output shares a net with input T. Stock Digital 0.31: the enabled Driver turns the floating input into a random DRIVEN output and burns against T about half the time. Patched: the output stays high-Z, T wins, never burns.
module driver_z2 (
  input  SD,
  input  SD2,
  input  S,
  input  T,
  output RESULT,
  output NOISE
);

  wire driver_1_out;

  assign driver_1_out = SD2 ? SD : 1'bz;  // Driver driver_1
  assign T = S ? driver_1_out : 1'bz;  // Driver driver_2
  not not_1 (NOISE, driver_1_out);

  assign RESULT = T;
endmodule
